// Digital circuit 16 bit BCD.dig as structural Verilog
module _16_bit_BCD (
  input  Cycle_Full,
  input  [15:0] Bin_IN,
  input  in_7,
  output [3:0] BCD_Digit,
  output [15:0] out_4,
  output [3:0] out_5,
  output MSB_CARRY,
  output [3:0] out_8,
  output [3:0] out_9,
  output [3:0] out_10,
  output [3:0] out_11
);

  wire A1, A2, A3, A4, A5, ALG_Finish, and_1_out, and_2_out, and_3_out, and_4_out, and_5_out, and_6_out,
       and_7_out, and_8_out, and_9_out, and_10_out, and_11_out, and_12_out, and_13_out, and_14_out,
       and_15_out, and_16_out, delay_2_out, delay_3_out, delay_4_out, delay_5_out, delay_6_out, delay_7_out,
       delay_8_out, delay_9_out, not_1_out, not_2_out, not_3_out, not_4_out, not_5_out, not_6_out, not_7_out,
       or_1_out, or_2_out, or_3_out, or_4_out, or_5_out, or_6_out, or_7_out, or_8_out, or_9_out, or_10_out,
       or_11_out, or_12_out, or_14_out, or_17_out, or_19_out, or_20_out, pulldown_35_out, pulldown_36_out,
       pulldown_37_out, pulldown_38_out, pulldown_39_out, pulldown_40_out, pulldown_41_out, pulldown_42_out,
       pulldown_45_out, pulldown_47_out, pulldown_48_out, pulldown_49_out, xor_1_out, xor_2_out, xor_3_out,
       xor_4_out, xor_5_out, xor_6_out;
  wire [0:0] Binary_Shift_OUT;
  wire [3:0] _16bitadder_1_sum, _16bitadder_2_sum, _16bitadder_3_sum, _16bitadder_4_sum, _16bitadder_5_sum,
       Bin_REG, Bin_REG_2, Bin_REG_3, Bin_REG_4, Bin_REG_5, multiplexer_6_out, multiplexer_7_out,
       multiplexer_8_out, multiplexer_10_out, multiplexer_11_out, pulldown_32_out, pulldown_33_out,
       pulldown_34_out, pulldown_44_out, pulldown_46_out;
  wire [15:0] multiplexer_9_out;
  wire [15:4] _16bitadder_1_sum_2, _16bitadder_2_sum_2, _16bitadder_3_sum_2, _16bitadder_4_sum_2,
       _16bitadder_5_sum_2, pulldown_1_out, pulldown_4_out, pulldown_7_out, pulldown_10_out, pulldown_13_out,
       pulldown_16_out, pulldown_19_out, pulldown_22_out, pulldown_25_out, pulldown_28_out;

  PullDown #(.Bits(4)) pulldown_1 (.out(pulldown_1_out[7:4]));
  PullDown #(.Bits(4)) pulldown_2 (.out(pulldown_1_out[11:8]));
  PullDown #(.Bits(4)) pulldown_3 (.out(pulldown_1_out[15:12]));
  PullDown #(.Bits(4)) pulldown_4 (.out(pulldown_4_out[7:4]));
  PullDown #(.Bits(4)) pulldown_5 (.out(pulldown_4_out[11:8]));
  PullDown #(.Bits(4)) pulldown_6 (.out(pulldown_4_out[15:12]));
  PullDown #(.Bits(4)) pulldown_7 (.out(pulldown_7_out[7:4]));
  PullDown #(.Bits(4)) pulldown_8 (.out(pulldown_7_out[11:8]));
  PullDown #(.Bits(4)) pulldown_9 (.out(pulldown_7_out[15:12]));
  PullDown #(.Bits(4)) pulldown_10 (.out(pulldown_10_out[7:4]));
  PullDown #(.Bits(4)) pulldown_11 (.out(pulldown_10_out[11:8]));
  PullDown #(.Bits(4)) pulldown_12 (.out(pulldown_10_out[15:12]));
  PullDown #(.Bits(4)) pulldown_13 (.out(pulldown_13_out[7:4]));
  PullDown #(.Bits(4)) pulldown_14 (.out(pulldown_13_out[11:8]));
  PullDown #(.Bits(4)) pulldown_15 (.out(pulldown_13_out[15:12]));
  PullDown #(.Bits(4)) pulldown_16 (.out(pulldown_16_out[7:4]));
  PullDown #(.Bits(4)) pulldown_17 (.out(pulldown_16_out[11:8]));
  PullDown #(.Bits(4)) pulldown_18 (.out(pulldown_16_out[15:12]));
  PullDown #(.Bits(4)) pulldown_19 (.out(pulldown_19_out[7:4]));
  PullDown #(.Bits(4)) pulldown_20 (.out(pulldown_19_out[11:8]));
  PullDown #(.Bits(4)) pulldown_21 (.out(pulldown_19_out[15:12]));
  PullDown #(.Bits(4)) pulldown_22 (.out(pulldown_22_out[7:4]));
  PullDown #(.Bits(4)) pulldown_23 (.out(pulldown_22_out[11:8]));
  PullDown #(.Bits(4)) pulldown_24 (.out(pulldown_22_out[15:12]));
  PullDown #(.Bits(4)) pulldown_25 (.out(pulldown_25_out[7:4]));
  PullDown #(.Bits(4)) pulldown_26 (.out(pulldown_25_out[11:8]));
  PullDown #(.Bits(4)) pulldown_27 (.out(pulldown_25_out[15:12]));
  PullDown #(.Bits(4)) pulldown_28 (.out(pulldown_28_out[7:4]));
  PullDown #(.Bits(4)) pulldown_29 (.out(pulldown_28_out[11:8]));
  PullDown #(.Bits(4)) pulldown_30 (.out(pulldown_28_out[15:12]));
  or or_1 (or_1_out, out_4[15], out_5[0]);
  or or_2 (or_2_out, out_5[1], out_5[2]);
  _16BitAdder _16bitadder_1 (
    .A({pulldown_16_out, out_5[2:0], out_4[15]}), .B({pulldown_1_out, 4'b0011}),
    .Sum({_16bitadder_1_sum_2, _16bitadder_1_sum}));  // open: Of
  or or_3 (or_3_out, out_5[3], out_8[0]);
  or or_4 (or_4_out, out_8[1], out_8[2]);
  _16BitAdder _16bitadder_2 (
    .A({pulldown_19_out, out_8[2:0], out_5[3]}), .B({pulldown_4_out, 4'b0011}),
    .Sum({_16bitadder_2_sum_2, _16bitadder_2_sum}));  // open: Of
  or or_5 (or_5_out, out_8[3], out_9[0]);
  or or_6 (or_6_out, out_9[1], out_9[2]);
  _16BitAdder _16bitadder_3 (
    .A({pulldown_22_out, out_9[2:0], out_8[3]}), .B({pulldown_7_out, 4'b0011}),
    .Sum({_16bitadder_3_sum_2, _16bitadder_3_sum}));  // open: Of
  or or_7 (or_7_out, out_9[3], out_11[0]);
  or or_8 (or_8_out, out_11[1], out_11[2]);
  _16BitAdder _16bitadder_4 (
    .A({pulldown_25_out, out_11[2:0], out_9[3]}), .B({pulldown_10_out, 4'b0011}),
    .Sum({_16bitadder_4_sum_2, _16bitadder_4_sum}));  // open: Of
  or or_9 (or_9_out, out_11[3], out_10[0]);
  or or_10 (or_10_out, out_10[1], out_10[2]);
  _16BitAdder _16bitadder_5 (
    .A({pulldown_28_out, out_10[2:0], out_11[3]}), .B({pulldown_13_out, 4'b0011}),
    .Sum({_16bitadder_5_sum_2, _16bitadder_5_sum}));  // open: Of
  not not_1 (not_1_out, A1);
  and and_1 (and_1_out, or_1_out, or_2_out);
  Multiplexer #(.Bits(4)) multiplexer_1 (
    .sel(and_6_out), .in_0({out_5[2:0], out_4[15]}), .in_1(_16bitadder_1_sum), .out(Bin_REG));
  not not_2 (not_2_out, A2);
  and and_2 (and_2_out, or_3_out, or_4_out);
  Multiplexer #(.Bits(4)) multiplexer_2 (
    .sel(and_7_out), .in_0({out_8[2:0], out_5[3]}), .in_1(_16bitadder_2_sum), .out(Bin_REG_2));
  not not_3 (not_3_out, A3);
  and and_3 (and_3_out, or_5_out, or_6_out);
  Multiplexer #(.Bits(4)) multiplexer_3 (
    .sel(and_8_out), .in_0({out_9[2:0], out_8[3]}), .in_1(_16bitadder_3_sum), .out(Bin_REG_3));
  not not_4 (not_4_out, A4);
  and and_4 (and_4_out, or_7_out, or_8_out);
  Multiplexer #(.Bits(4)) multiplexer_4 (
    .sel(and_9_out), .in_0({out_11[2:0], out_9[3]}), .in_1(_16bitadder_4_sum), .out(Bin_REG_4));
  not not_5 (not_5_out, A5);
  and and_5 (and_5_out, or_9_out, or_10_out);
  Multiplexer #(.Bits(4)) multiplexer_5 (
    .sel(and_10_out), .in_0({out_10[2:0], out_11[3]}), .in_1(_16bitadder_5_sum), .out(Bin_REG_5));
  and and_6 (and_6_out, not_1_out, and_1_out);
  and and_7 (and_7_out, not_2_out, and_2_out);
  and and_8 (and_8_out, not_3_out, and_3_out);
  and and_9 (and_9_out, not_4_out, and_4_out);
  and and_10 (and_10_out, not_5_out, and_5_out);
  and and_11 (and_11_out, or_11_out, out_10[2]);
  or or_11 (or_11_out, out_10[0], out_10[1]);
  or or_12 (or_12_out, out_4[7], out_4[0], out_4[1], out_4[2], out_4[3], out_4[4], out_4[5], out_4[6], out_4[8], out_4[9], out_4[10], out_4[11], out_4[12], out_4[13], out_4[14], out_4[15]);
  or or_13 (A5, and_11_out, MSB_CARRY);
  or or_14 (or_14_out, out_11[0], out_11[1]);
  PullDown pulldown_31 (.out(Binary_Shift_OUT[0]));
  or or_15 (A4, and_12_out, out_11[3]);
  and and_12 (and_12_out, or_14_out, out_11[2]);
  Delay delay_1 (.in(not_6_out), .out(ALG_Finish));
  not not_6 (not_6_out, or_12_out);
  or or_16 (A3, and_13_out, out_9[3]);
  and and_13 (and_13_out, or_17_out, out_9[2]);
  or or_17 (or_17_out, out_9[0], out_9[1]);
  or or_18 (A2, and_14_out, out_8[3]);
  and and_14 (and_14_out, or_19_out, out_8[2]);
  or or_19 (or_19_out, out_8[0], out_8[1]);
  and and_15 (and_15_out, or_20_out, out_5[2]);
  or or_20 (or_20_out, out_5[0], out_5[1]);
  or or_21 (A1, and_15_out, out_5[3]);
  not not_7 (not_7_out, ALG_Finish);
  and and_16 (and_16_out, not_7_out, in_7);
  Delay delay_2 (.in(and_16_out), .out(delay_2_out));
  Delay #(.delayTime(5)) delay_3 (.in(and_16_out), .out(delay_3_out));
  PullDown #(.Bits(4)) pulldown_32 (.out(pulldown_32_out));
  Multiplexer #(.Bits(4)) multiplexer_6 (
    .sel(delay_6_out), .in_0(pulldown_32_out), .in_1(Bin_REG), .out(multiplexer_6_out));
  PullDown #(.Bits(4)) pulldown_33 (.out(pulldown_33_out));
  Multiplexer #(.Bits(4)) multiplexer_7 (
    .sel(delay_7_out), .in_0(pulldown_33_out), .in_1(Bin_REG_2), .out(multiplexer_7_out));
  PullDown #(.Bits(4)) pulldown_34 (.out(pulldown_34_out));
  Multiplexer #(.Bits(4)) multiplexer_8 (
    .sel(delay_4_out), .in_0(pulldown_34_out), .in_1(Bin_REG_3), .out(multiplexer_8_out));
  Delay delay_4 (.in(Cycle_Full), .out(delay_4_out));
  Multiplexer #(.Bits(16)) multiplexer_9 (
    .sel(delay_5_out), .in_0(Bin_IN), .in_1({out_4[14:0], Binary_Shift_OUT[0]}), .out(multiplexer_9_out));
  PullDown pulldown_35 (.out(pulldown_35_out));
  Delay #(.delayTime(2)) delay_5 (.in(Cycle_Full), .out(delay_5_out));
  xor xor_1 (xor_1_out, pulldown_36_out, pulldown_40_out);
  PullDown pulldown_36 (.out(pulldown_36_out));
  DiodeForward diodeforward_1 (.in(delay_3_out), .out(pulldown_36_out));
  Delay delay_6 (.in(Cycle_Full), .out(delay_6_out));
  xor xor_2 (xor_2_out, pulldown_37_out, pulldown_41_out);
  PullDown pulldown_37 (.out(pulldown_37_out));
  DiodeForward diodeforward_2 (.in(delay_3_out), .out(pulldown_37_out));
  Delay delay_7 (.in(Cycle_Full), .out(delay_7_out));
  xor xor_3 (xor_3_out, pulldown_38_out, pulldown_42_out);
  PullDown pulldown_38 (.out(pulldown_38_out));
  DiodeForward diodeforward_3 (.in(delay_3_out), .out(pulldown_38_out));
  xor xor_4 (xor_4_out, pulldown_35_out, pulldown_39_out);
  PullDown pulldown_39 (.out(pulldown_39_out));
  DiodeForward diodeforward_4 (.in(Cycle_Full), .out(pulldown_39_out));
  DiodeForward diodeforward_5 (.in(delay_2_out), .out(pulldown_35_out));
  PullDown pulldown_40 (.out(pulldown_40_out));
  DiodeForward diodeforward_6 (.in(Cycle_Full), .out(pulldown_40_out));
  PullDown pulldown_41 (.out(pulldown_41_out));
  DiodeForward diodeforward_7 (.in(Cycle_Full), .out(pulldown_41_out));
  PullDown pulldown_42 (.out(pulldown_42_out));
  DiodeForward diodeforward_8 (.in(Cycle_Full), .out(pulldown_42_out));
  PullDown #(.Bits(4)) pulldown_43 (.out(BCD_Digit));
  Register #(.Bits(4)) register_1 (.D(multiplexer_6_out), .C(xor_1_out), .en(Cycle_Full), .Q(out_5));
  Register #(.Bits(4)) register_2 (.D(multiplexer_7_out), .C(xor_2_out), .en(Cycle_Full), .Q(out_8));
  Register #(.Bits(4)) register_3 (.D(multiplexer_8_out), .C(xor_3_out), .en(Cycle_Full), .Q(out_9));
  Register #(.Bits(16)) register_4 (.D(multiplexer_9_out), .C(xor_4_out), .en(Cycle_Full), .Q(out_4));
  PullDown #(.Bits(4)) pulldown_44 (.out(pulldown_44_out));
  Multiplexer #(.Bits(4)) multiplexer_10 (
    .sel(delay_8_out), .in_0(pulldown_44_out), .in_1(Bin_REG_4), .out(multiplexer_10_out));
  PullDown pulldown_45 (.out(pulldown_45_out));
  Delay delay_8 (.in(Cycle_Full), .out(delay_8_out));
  PullDown #(.Bits(4)) pulldown_46 (.out(pulldown_46_out));
  Multiplexer #(.Bits(4)) multiplexer_11 (
    .sel(delay_9_out), .in_0(pulldown_46_out), .in_1(Bin_REG_5), .out(multiplexer_11_out));
  Delay delay_9 (.in(Cycle_Full), .out(delay_9_out));
  xor xor_5 (xor_5_out, pulldown_45_out, pulldown_47_out);
  PullDown pulldown_47 (.out(pulldown_47_out));
  DiodeForward diodeforward_9 (.in(Cycle_Full), .out(pulldown_47_out));
  DiodeForward diodeforward_10 (.in(delay_3_out), .out(pulldown_45_out));
  xor xor_6 (xor_6_out, pulldown_48_out, pulldown_49_out);
  PullDown pulldown_48 (.out(pulldown_48_out));
  DiodeForward diodeforward_11 (.in(delay_3_out), .out(pulldown_48_out));
  PullDown pulldown_49 (.out(pulldown_49_out));
  DiodeForward diodeforward_12 (.in(Cycle_Full), .out(pulldown_49_out));
  Register #(.Bits(4)) register_5 (.D(multiplexer_10_out), .C(xor_5_out), .en(Cycle_Full), .Q(out_11));
  Register #(.Bits(4)) register_6 (
    .D(multiplexer_11_out), .C(xor_6_out), .en(Cycle_Full), .Q({MSB_CARRY, out_10[2:0]}));

  assign out_10[3] = MSB_CARRY;

  // Other names for the same wires on the sheet: Binary_Load_IN[3:0] = out_5;
  //   Binary_Load_OUT[3:0] = {out_5[2:0], out_4[15]}; Binary_Load_OUT_2[3:0] = {out_8[2:0], out_5[3]};
  //   Process_BIT_2 = out_5[3]; Binary_Load_IN_2[3:0] = out_8; Binary_Load_OUT_3[3:0] = {out_9[2:0], out_8[3]};
  //   Process_BIT_3 = out_8[3]; Binary_Load_IN_3[3:0] = out_9; Binary_Load_OUT_4[3:0] = {out_11[2:0], out_9[3]};
  //   Process_BIT_4 = out_9[3]; Binary_Load_IN_4[3:0] = out_11; Binary_Load_OUT_5[3:0] = {out_10[2:0], out_11[3]};
  //   Process_BIT_5 = out_11[3]; Binary_Load_IN_5[3:0] = {MSB_CARRY, out_10[2:0]}; Binary_Shift_IN[15:0] = out_4;
  //   Binary_Shift_OUT[15:1] = out_4[14:0]; Process_BIT = out_4[15]; Cycle_Early = Cycle_Full
endmodule
