// Digital circuit 16 bit Shift.dig as structural Verilog
module _16_bit_Shift (
  input  [15:0] Shift_In,
  output Process_bit,
  output [15:0] Shift_out
);

  PullDown pulldown_1 (.out(Shift_out[0]));

  assign Process_bit = Shift_In[15];
  assign Shift_out[15:1] = Shift_In[14:0];
endmodule
