// Digital circuit 16Bbit Clr.dig as structural Verilog
module _16Bbit_Clr (
  input  [15:0] CLR,
  input  Cycle_in,
  output [15:0] Reg_A_CLEAR,
  output [15:0] Reg_B_CLEAR,
  output [15:0] CLR_Mux,
  output Cycle_Out
);

  and and_1 (Cycle_Out, Cycle_in, CLR[0]);
  PullDown #(.Bits(4)) pulldown_1 (.out(Reg_A_CLEAR[15:12]));
  // Pins of 1 and 16 bits meet at CLR

  assign CLR_Mux = CLR;
  assign Reg_A_CLEAR[11:0] = {Reg_A_CLEAR[15:12], Reg_A_CLEAR[15:12], Reg_A_CLEAR[15:12]};
  assign Reg_B_CLEAR = {Reg_A_CLEAR[15:12], Reg_A_CLEAR[15:12], Reg_A_CLEAR[15:12], Reg_A_CLEAR[15:12]};
endmodule
