// Digital circuit 16Bit decode 5bit.dig as structural Verilog
module _16Bit_decode_5bit (
  input  [4:0] I,
  output _0Cycle,
  output [15:0] Binary_OUT
);

  wire _1bitadder_1_carry, _1bitadder_2_carry, _1bitadder_2_sum, _1bitadder_3_carry, _1bitadder_4_sum,
       _16bit_calc_equals_1_eq, _16bit_calc_plus_decode_1_plus, _16bit_calc_subtract_decode_1_out_2,
       and_1_out, and_2_out, and_3_out, and_4_out, and_5_out, and_6_out, not_1_out, not_2_out, not_3_out,
       or_1_out, or_2_out, or_3_out;

  _16bit_Calc_Equals _16bit_calc_equals_1 (.I(I), .eq(_16bit_calc_equals_1_eq));
  _16bit_Calc_Plus_Decode _16bit_calc_plus_decode_1 (.I(I), .plus(_16bit_calc_plus_decode_1_plus));
  _16bit_Calc_Subtract_Decode _16bit_calc_subtract_decode_1 (.I(I), .out_2(_16bit_calc_subtract_decode_1_out_2));
  or or_1 (or_1_out, _16bit_calc_equals_1_eq, _16bit_calc_plus_decode_1_plus);
  or or_2 (or_2_out, or_1_out, _16bit_calc_subtract_decode_1_out_2);
  or or_3 (or_3_out, I[4], or_2_out);
  not not_1 (not_1_out, or_3_out);
  and and_1 (and_1_out, I[3], not_1_out);
  and and_2 (and_2_out, I[2], not_1_out);
  and and_3 (and_3_out, I[1], not_1_out);
  and and_4 (and_4_out, I[0], not_1_out);
  not not_2 (not_2_out, and_4_out);
  not not_3 (not_3_out, and_2_out);
  and and_5 (and_5_out, not_2_out, not_3_out);
  and and_6 (and_6_out, and_3_out, and_1_out);
  _1BitAdder _1bitadder_1 (.A(and_4_out), .B(1'b0), .C_IN(1'b0), .Sum(Binary_OUT[0]), .Carry(_1bitadder_1_carry));
  _1BitAdder _1bitadder_2 (
    .A(and_3_out), .B(1'b0), .C_IN(_1bitadder_1_carry), .Sum(_1bitadder_2_sum), .Carry(_1bitadder_2_carry));
  and and_7 (_0Cycle, and_6_out, and_5_out);
  _1BitAdder _1bitadder_3 (
    .A(and_2_out), .B(1'b0), .C_IN(_1bitadder_2_carry), .Sum(Binary_OUT[2]), .Carry(_1bitadder_3_carry));
  _1BitAdder _1bitadder_4 (.A(and_1_out), .B(1'b0), .C_IN(_1bitadder_3_carry), .Sum(_1bitadder_4_sum));  // open: Carry
  xor xor_1 (Binary_OUT[1], _0Cycle, _1bitadder_2_sum);
  xor xor_2 (Binary_OUT[3], _1bitadder_4_sum, _0Cycle);
  PullDown pulldown_1 (.out(Binary_OUT[15]));

  assign Binary_OUT[14:4] = {11{Binary_OUT[15]}};
endmodule
