// Digital circuit 16BitAdder.dig as structural Verilog
module _16BitAdder (
  input  [15:0] A,
  input  [15:0] B,
  output Of,
  output [15:0] Sum
);

  wire Carry1, Carry2, Carry3, Carry4, Carry5, Carry6, Carry7, Carry8, Carry9, Carry10, Carry11, Carry12,
       Carry13, Carry14, Carry15;

  _1BitAdder _1bitadder_1 (.A(A[0]), .B(B[0]), .C_IN(1'b0), .Sum(Sum[0]), .Carry(Carry1));
  _1BitAdder _1bitadder_2 (.A(A[1]), .B(B[1]), .C_IN(Carry1), .Sum(Sum[1]), .Carry(Carry2));
  _1BitAdder _1bitadder_3 (.A(A[2]), .B(B[2]), .C_IN(Carry2), .Sum(Sum[2]), .Carry(Carry3));
  _1BitAdder _1bitadder_4 (.A(A[3]), .B(B[3]), .C_IN(Carry3), .Sum(Sum[3]), .Carry(Carry4));
  _1BitAdder _1bitadder_5 (.A(A[4]), .B(B[4]), .C_IN(Carry4), .Sum(Sum[4]), .Carry(Carry5));
  _1BitAdder _1bitadder_6 (.A(A[5]), .B(B[5]), .C_IN(Carry5), .Sum(Sum[5]), .Carry(Carry6));
  _1BitAdder _1bitadder_7 (.A(A[6]), .B(B[6]), .C_IN(Carry6), .Sum(Sum[6]), .Carry(Carry7));
  _1BitAdder _1bitadder_8 (.A(A[7]), .B(B[7]), .C_IN(Carry7), .Sum(Sum[7]), .Carry(Carry8));
  _1BitAdder _1bitadder_9 (.A(A[8]), .B(B[8]), .C_IN(Carry8), .Sum(Sum[8]), .Carry(Carry9));
  _1BitAdder _1bitadder_10 (.A(A[9]), .B(B[9]), .C_IN(Carry9), .Sum(Sum[9]), .Carry(Carry10));
  _1BitAdder _1bitadder_11 (.A(A[10]), .B(B[10]), .C_IN(Carry10), .Sum(Sum[10]), .Carry(Carry11));
  _1BitAdder _1bitadder_12 (.A(A[11]), .B(B[11]), .C_IN(Carry11), .Sum(Sum[11]), .Carry(Carry12));
  _1BitAdder _1bitadder_13 (.A(A[12]), .B(B[12]), .C_IN(Carry12), .Sum(Sum[12]), .Carry(Carry13));
  _1BitAdder _1bitadder_14 (.A(A[13]), .B(B[13]), .C_IN(Carry13), .Sum(Sum[13]), .Carry(Carry14));
  _1BitAdder _1bitadder_15 (.A(A[14]), .B(B[14]), .C_IN(Carry14), .Sum(Sum[14]), .Carry(Carry15));
  _1BitAdder _1bitadder_16 (.A(A[15]), .B(B[15]), .C_IN(Carry15), .Sum(Sum[15]), .Carry(Of));

  // Other names for the same wires on the sheet: Output_9_16[7:0] = Sum[15:8]; InputA1 = A[0]; InputA2 = A[1];
  //   InputA3 = A[2]; InputA4 = A[3]; InputA5 = A[4]; InputA6 = A[5]; InputA7 = A[6]; InputA8 = A[7]; InputA9 = A[8];
  //   InputA10 = A[9]; InputA11 = A[10]; InputA12 = A[11]; InputA13 = A[12]; InputA14 = A[13]; InputA15 = A[14];
  //   InputA16 = A[15]; InputB1 = B[0]; InputB2 = B[1]; InputB3 = B[2]; InputB4 = B[3]; InputB5 = B[4];
  //   InputB6 = B[5]; InputB7 = B[6]; InputB8 = B[7]; InputB9 = B[8]; InputB10 = B[9]; InputB11 = B[10];
  //   InputB12 = B[11]; InputB13 = B[12]; InputB14 = B[13]; InputB15 = B[14]; InputB16 = B[15]

  // Notes on the sheet:
  //   A: Secondary input for adding 2 integers
  //   B: Secondary input for adding 2 integers
  //   Of: Overflow
  //   Sum: Product of 2 integers
endmodule
