// Digital circuit 16BitInverter.dig as structural Verilog
module _16BitInverter (
  input  [15:0] I,
  output [15:0] O
);

  wire [15:0] not_1_out, pullup_1_out;

  assign not_1_out = ~I;  // Not not_1, 16 bits wide
  PullUp pullup_1 (.out(pullup_1_out[0]));
  PullDown pulldown_1 (.out(pullup_1_out[15]));
  _16BitAdder _16bitadder_1 (.A(not_1_out), .B({{15{pullup_1_out[15]}}, pullup_1_out[0]}), .Sum(O));  // open: Of
endmodule
