// Digital circuit 16bit Calc ALU.dig as structural Verilog
module _16bit_Calc_ALU (
  input  Add,
  input  Sub,
  input  [15:0] Reg_A,
  input  [15:0] Reg_B,
  input  Cycle_In,
  input  Clear,
  output [15:0] Reg_B_OUT,
  output Cycle_Out,
  output [15:0] Reg_A_OUT
);

  wire and_1_out, diodeforward_1_out;
  wire [15:0] _16bit_subtractor_1_y, _16bitadder_1_sum, multiplexer_1_out, multiplexer_2_out;

  _16BitAdder _16bitadder_1 (.A(Reg_A), .B(Reg_B), .Sum(_16bitadder_1_sum));  // open: Of
  _16bit_Subtractor _16bit_subtractor_1 (.A(Reg_A), .B(Reg_B), .Y(_16bit_subtractor_1_y));
  Multiplexer #(.Bits(16)) multiplexer_1 (
    .sel(Add), .in_0({16{1'b0}}), .in_1(_16bitadder_1_sum), .out(multiplexer_1_out));
  DiodeForward diodeforward_1 (.in(Add), .out(diodeforward_1_out));
  Multiplexer #(.Bits(16)) multiplexer_2 (
    .sel(Sub), .in_0({16{1'b0}}), .in_1(_16bit_subtractor_1_y), .out(multiplexer_2_out));
  DiodeForward diodeforward_2 (.in(Sub), .out(diodeforward_1_out));
  DiodeForward diodeforward_3 (.in(Clear), .out(diodeforward_1_out));
  assign Reg_B_OUT = multiplexer_1_out | multiplexer_2_out;  // Or or_1, 16 bits wide
  PullDown pulldown_1 (.out(diodeforward_1_out));
  and and_1 (and_1_out, Cycle_In, diodeforward_1_out);
  Delay #(.delayTime(3)) delay_1 (.in(and_1_out), .out(Cycle_Out));

  assign Reg_A_OUT = {16{1'b0}};
endmodule
