// Digital circuit 16bit Calc CLR.dig as structural Verilog
module _16bit_Calc_CLR (
  input  [4:0] I,
  output CLR
);

  wire and_1_out, and_2_out, not_1_out, or_1_out;

  or or_1 (or_1_out, I[0], I[1]);
  and and_1 (and_1_out, I[3], I[4]);
  and and_2 (and_2_out, I[2], and_1_out);
  not not_1 (not_1_out, or_1_out);
  and and_3 (CLR, not_1_out, and_2_out);
endmodule
