// Digital circuit 16bit Calc Equals.dig as structural Verilog
module _16bit_Calc_Equals (
  input  [4:0] I,
  output eq
);

  wire and_1_out, not_1_out, or_1_out, or_2_out;

  or or_1 (or_1_out, I[0], I[1]);
  and and_1 (and_1_out, I[3], I[4]);
  or or_2 (or_2_out, or_1_out, I[2]);
  not not_1 (not_1_out, or_2_out);
  and and_2 (eq, not_1_out, and_1_out);
endmodule
