// Digital circuit 16bit Calc Plus Decode.dig as structural Verilog
module _16bit_Calc_Plus_Decode (
  input  [4:0] I,
  output plus
);

  wire not_1_out, or_1_out, or_2_out, or_3_out;

  or or_1 (or_1_out, I[0], I[1]);
  or or_2 (or_2_out, or_1_out, I[2]);
  or or_3 (or_3_out, or_2_out, I[3]);
  not not_1 (not_1_out, or_3_out);
  and and_1 (plus, not_1_out, I[4]);
endmodule
