// Digital circuit 16bit Calc Register A and B.dig as structural Verilog
module _16bit_Calc_Register_A_and_B (
  input  Cycle_In,
  input  Reg_A_Cycle,
  input  Reg_B_Cycle,
  input  Clear,
  input  [15:0] Reg_A_Binary,
  input  [15:0] Reg_B_Binary,
  output [15:0] Reg_A_OUT,
  output [15:0] Reg_B_OUT,
  output Cycle_Out
);

  wire and_1_out, delay_1_out, delay_2_out, or_1_out, or_2_out;
  wire [15:0] T1, T2;
  wire [15:15] pulldown_2_out;

  PullDown pulldown_1 (.out(Clear));
  and and_1 (and_1_out, Cycle_In, Clear);
  PullDown pulldown_2 (.out(pulldown_2_out[15]));
  Multiplexer #(.Bits(16)) multiplexer_1 (
    .sel(and_1_out), .in_0(Reg_A_Binary), .in_1({16{pulldown_2_out[15]}}), .out(T1));
  Multiplexer #(.Bits(16)) multiplexer_2 (
    .sel(and_1_out), .in_0(Reg_B_Binary), .in_1({16{pulldown_2_out[15]}}), .out(T2));
  PullDown #(.Bits(16)) pulldown_3 (.out({16{pulldown_2_out[15]}}));
  or or_1 (or_1_out, and_1_out, Reg_A_Cycle);
  or or_2 (or_2_out, and_1_out, Reg_B_Cycle);
  Delay delay_1 (.in(or_1_out), .out(delay_1_out));
  Delay delay_2 (.in(or_2_out), .out(delay_2_out));
  Delay #(.delayTime(5)) delay_3 (.in(and_1_out), .out(Cycle_Out));
  Register #(.Bits(16)) Reg_A (.D(T1), .C(delay_1_out), .en(Cycle_In), .Q(Reg_A_OUT));
  Register #(.Bits(16)) Reg_B (.D(T2), .C(delay_2_out), .en(Cycle_In), .Q(Reg_B_OUT));
endmodule
