// Digital circuit 16bit Calc Subtract Decode.dig as structural Verilog
module _16bit_Calc_Subtract_Decode (
  input  [4:0] I,
  output out_2
);

  wire and_1_out, not_1_out, or_1_out, or_2_out;

  or or_1 (or_1_out, I[0], I[1]);
  or or_2 (or_2_out, or_1_out, I[3]);
  and and_1 (and_1_out, I[2], I[4]);
  not not_1 (not_1_out, or_2_out);
  and and_2 (out_2, not_1_out, and_1_out);
endmodule
