// Digital circuit 16bit Key Cycle.dig as structural Verilog
module _16bit_Key_Cycle (
  input  [15:0] Binary,
  input  Cycle_In,
  input  [15:0] Reg_A_IN,
  output [15:0] Reg_A_OUT,
  output Cycle_OUT
);

  wire and_1_out, and_2_out, not_1_out, or_1_out, or_2_out, or_3_out;
  wire [15:0] _16bitadder_1_sum, mutllplier10bit16_1_o10x;
  wire [15:15] pulldown_1_out;

  Mutllplier10Bit16 mutllplier10bit16_1 (.K(Reg_A_IN), .O10x(mutllplier10bit16_1_o10x));
  _16BitAdder _16bitadder_1 (.A(mutllplier10bit16_1_o10x), .B(Binary), .Sum(_16bitadder_1_sum));  // open: Of
  or or_1 (or_1_out, Binary[0], Binary[1]);
  or or_2 (or_2_out, or_1_out, Binary[2]);
  or or_3 (or_3_out, or_2_out, Binary[3]);
  PullDown pulldown_1 (.out(pulldown_1_out[15]));
  Multiplexer #(.Bits(16)) multiplexer_1 (
    .sel(and_1_out), .in_0({16{pulldown_1_out[15]}}), .in_1(_16bitadder_1_sum), .out(Reg_A_OUT));
  and and_1 (and_1_out, Cycle_In, and_2_out);
  not not_1 (not_1_out, Binary[4]);
  and and_2 (and_2_out, or_3_out, not_1_out);
  Delay #(.delayTime(5)) delay_1 (.in(and_1_out), .out(Cycle_OUT));
endmodule
