// Digital circuit 16bit Subtractor.dig as structural Verilog
module _16bit_Subtractor (
  input  [15:0] A,
  input  [15:0] B,
  output [15:0] Y
);

  wire [15:0] _16bitinverter_1_o;

  _16BitInverter _16bitinverter_1 (.I(A), .O(_16bitinverter_1_o));
  _16BitAdder _16bitadder_1 (.A(_16bitinverter_1_o), .B(B), .Sum(Y));  // open: Of
endmodule
