// Digital circuit 1BitAdder.dig as structural Verilog
module _1BitAdder (
  input  A,
  input  B,
  input  C_IN,
  output Sum,
  output Carry
);

  wire and_1_out, and_2_out, xor_1_out;

  xor xor_1 (xor_1_out, A, B);
  and and_1 (and_1_out, A, B);
  xor xor_2 (Sum, C_IN, xor_1_out);
  and and_2 (and_2_out, xor_1_out, C_IN);
  or or_1 (Carry, and_1_out, and_2_out);
endmodule
