// Digital circuit 4bit OR.dig as structural Verilog
module _4bit_OR (
  input  [15:0] IF,
  output OUT
);

  wire or_1_out, or_2_out, or_3_out, or_4_out, or_5_out, or_6_out, or_7_out, or_8_out, or_9_out, or_10_out,
       or_11_out, or_12_out, or_13_out, or_14_out;

  or or_1 (or_1_out, IF[0], IF[1]);
  or or_2 (or_2_out, IF[4], IF[5]);
  or or_3 (or_3_out, IF[8], IF[9]);
  or or_4 (or_4_out, IF[12], IF[13]);
  or or_5 (or_5_out, or_1_out, IF[2]);
  or or_6 (or_6_out, or_2_out, IF[6]);
  or or_7 (or_7_out, or_3_out, IF[10]);
  or or_8 (or_8_out, or_4_out, IF[14]);
  or or_9 (or_9_out, or_5_out, IF[3]);
  or or_10 (or_10_out, or_6_out, IF[7]);
  or or_11 (or_11_out, or_7_out, IF[11]);
  or or_12 (or_12_out, or_8_out, IF[15]);
  or or_13 (or_13_out, or_9_out, or_10_out);
  or or_14 (or_14_out, or_11_out, or_12_out);
  or or_15 (OUT, or_13_out, or_14_out);
endmodule
