// Digital circuit ALU AND REG TIMING.dig as structural Verilog
module ALU_AND_REG_TIMING (
  output [15:0] out_1,
  output [15:0] out_2
);

  wire Add, ALU_Cycle, and_1_out, and_2_out, and_3_out, and_4_out, and_5_out, and_6_out, and_7_out,
       and_8_out, and_9_out, and_10_out, and_11_out, and_12_out, and_13_out, and_14_out, and_15_out,
       and_16_out, and_17_out, and_18_out, and_19_out, and_20_out, and_21_out, and_22_out, and_23_out,
       and_24_out, and_25_out, and_26_out, and_27_out, and_28_out, and_29_out, and_30_out, and_31_out,
       and_32_out, and_33_out, and_34_out, Carry1, Carry2, Carry3, Carry4, Carry5, Carry6, Carry7, Carry8,
       Carry9, Carry10, Carry11, Carry12, Carry13, Carry14, Carry15, Clear, Cycle_1, Cycle_3, delay_1_out,
       delay_2_out, delay_4_out, delay_5_out, delay_6_out, diodeforward_1_out, diodeforward_4_out,
       diodeforward_5_out, InputA1, InputA2, InputA3, InputA4, InputA5, InputA6, InputA7, InputA8, InputA9,
       InputA10, InputA11, InputA12, InputA13, InputA14, InputA15, InputA16, InputB1, InputB2, InputB3,
       InputB4, InputB5, InputB6, InputB7, InputB8, InputB9, InputB10, InputB11, InputB12, InputB13,
       InputB14, InputB15, InputB16, or_10_out, or_11_out, or_19_out, Shift_Cycle, Sub, xor_1_out, xor_2_out,
       xor_3_out, xor_4_out, xor_5_out, xor_6_out, xor_7_out, xor_8_out, xor_17_out, xor_18_out, xor_19_out,
       xor_20_out, xor_21_out, xor_22_out, xor_23_out, xor_24_out;
  wire [1:0] ALU_MUX;
  wire [7:0] Output_9_16, xor_9_out;
  wire [15:0] ALU_B, multiplexer_3_out, multiplexer_4_out, multiplexer_6_out, multiplexer_7_out, not_1_out,
       pulldown_1_out, pulldown_2_out, pulldown_4_out, Reg_A_In, S, subtracted, T1, Temp_in, Temp_out;

  PullDown #(.Bits(16)) pulldown_1 (.out(pulldown_1_out));
  assign not_1_out = ~out_1;  // Not not_1, 16 bits wide
  PullDown #(.Bits(16)) pulldown_2 (.out(pulldown_2_out));
  Multiplexer #(.Selector_Bits(2), .Bits(16)) multiplexer_1 (
    .sel(ALU_MUX), .in_0(out_1), .in_1(pulldown_1_out), .in_2(not_1_out), .in_3(Temp_out),
    .out({InputA16, InputA15, InputA14, InputA13, InputA12, InputA11, InputA10, InputA9, InputA8, InputA7, InputA6, InputA5, InputA4, InputA3, InputA2, InputA1}));
  Multiplexer #(.Selector_Bits(2), .Bits(16)) multiplexer_2 (
    .sel(ALU_MUX), .in_0(out_2), .in_1(pulldown_2_out), .in_2({16{1'b1}}), .in_3(out_2),
    .out({InputB16, InputB15, InputB14, InputB13, InputB12, InputB11, InputB10, InputB9, InputB8, InputB7, InputB6, InputB5, InputB4, InputB3, InputB2, InputB1}));
  xor xor_1 (xor_1_out, InputA1, InputB1);
  and and_1 (and_1_out, InputA1, InputB1);
  xor xor_2 (xor_2_out, InputA2, InputB2);
  and and_2 (and_2_out, InputA2, InputB2);
  xor xor_3 (xor_3_out, InputA3, InputB3);
  and and_3 (and_3_out, InputA3, InputB3);
  xor xor_4 (xor_4_out, InputA4, InputB4);
  and and_4 (and_4_out, InputA4, InputB4);
  xor xor_5 (xor_5_out, InputA5, InputB5);
  and and_5 (and_5_out, InputA5, InputB5);
  xor xor_6 (xor_6_out, InputA6, InputB6);
  and and_6 (and_6_out, InputA6, InputB6);
  xor xor_7 (xor_7_out, InputA7, InputB7);
  and and_7 (and_7_out, InputA7, InputB7);
  xor xor_8 (xor_8_out, InputA8, InputB8);
  and and_8 (and_8_out, InputA8, InputB8);
  Delay #(.delayTime(2)) delay_1 (.in(Add), .out(delay_1_out));
  Delay #(.delayTime(20)) delay_2 (.in(Sub), .out(delay_2_out));
  xor xor_9 (xor_9_out[0], 1'b0, xor_1_out);
  and and_9 (and_9_out, xor_1_out, 1'b0);
  xor xor_10 (xor_9_out[1], Carry1, xor_2_out);
  and and_10 (and_10_out, xor_2_out, Carry1);
  xor xor_11 (xor_9_out[2], Carry2, xor_3_out);
  and and_11 (and_11_out, xor_3_out, Carry2);
  xor xor_12 (xor_9_out[3], Carry3, xor_4_out);
  and and_12 (and_12_out, xor_4_out, Carry3);
  xor xor_13 (xor_9_out[4], Carry4, xor_5_out);
  and and_13 (and_13_out, xor_5_out, Carry4);
  xor xor_14 (xor_9_out[5], Carry5, xor_6_out);
  and and_14 (and_14_out, xor_6_out, Carry5);
  xor xor_15 (xor_9_out[6], Carry6, xor_7_out);
  and and_15 (and_15_out, xor_7_out, Carry6);
  xor xor_16 (xor_9_out[7], Carry7, xor_8_out);
  and and_16 (and_16_out, xor_8_out, Carry7);
  Multiplexer #(.Bits(16)) multiplexer_3 (.sel(delay_1_out), .in_0({16{1'b0}}), .in_1(S), .out(multiplexer_3_out));
  DiodeForward diodeforward_1 (.in(delay_1_out), .out(diodeforward_1_out));
  Multiplexer #(.Bits(16)) multiplexer_4 (
    .sel(delay_2_out), .in_0({16{1'b0}}), .in_1(subtracted), .out(multiplexer_4_out));
  DiodeForward diodeforward_2 (.in(delay_2_out), .out(diodeforward_1_out));
  DiodeForward diodeforward_3 (.in(Clear), .out(diodeforward_1_out));
  or or_1 (Carry1, and_1_out, and_9_out);
  or or_2 (Carry2, and_2_out, and_10_out);
  or or_3 (Carry3, and_3_out, and_11_out);
  or or_4 (Carry4, and_4_out, and_12_out);
  or or_5 (Carry5, and_5_out, and_13_out);
  or or_6 (Carry6, and_6_out, and_14_out);
  or or_7 (Carry7, and_7_out, and_15_out);
  or or_8 (Carry8, and_8_out, and_16_out);
  assign ALU_B = multiplexer_3_out | multiplexer_4_out;  // Or or_9, 16 bits wide
  PullDown pulldown_3 (.out(diodeforward_1_out));
  and and_17 (and_17_out, Cycle_1, diodeforward_1_out);
  Delay #(.delayTime(3)) delay_3 (.in(and_17_out), .out(ALU_Cycle));
  PullDown #(.Bits(16)) pulldown_4 (.out(pulldown_4_out));
  Demultiplexer #(.Selector_Bits(2), .Bits(16)) demultiplexer_1 (
    .sel(ALU_MUX), .in({Output_9_16, xor_9_out}), .out_0(S), .out_1(pulldown_4_out), .out_2(Temp_in),
    .out_3(subtracted));
  Multiplexer #(.Bits(16)) multiplexer_5 (.sel(or_11_out), .in_0(Reg_A_In), .in_1({16{1'b0}}), .out(T1));
  or or_10 (or_10_out, Shift_Cycle, ALU_Cycle);
  and and_18 (and_18_out, ALU_Cycle, or_11_out);
  or or_11 (or_11_out, Add, Sub);
  DiodeForward diodeforward_4 (.in(or_10_out), .out(diodeforward_4_out));
  Delay delay_4 (.in(and_18_out), .out(delay_4_out));
  xor xor_17 (xor_17_out, InputA9, InputB9);
  and and_19 (and_19_out, InputA9, InputB9);
  xor xor_18 (xor_18_out, InputA10, InputB10);
  and and_20 (and_20_out, InputA10, InputB10);
  xor xor_19 (xor_19_out, InputA11, InputB11);
  and and_21 (and_21_out, InputA11, InputB11);
  xor xor_20 (xor_20_out, InputA12, InputB12);
  and and_22 (and_22_out, InputA12, InputB12);
  xor xor_21 (xor_21_out, InputA13, InputB13);
  and and_23 (and_23_out, InputA13, InputB13);
  xor xor_22 (xor_22_out, InputA14, InputB14);
  and and_24 (and_24_out, InputA14, InputB14);
  xor xor_23 (xor_23_out, InputA15, InputB15);
  and and_25 (and_25_out, InputA15, InputB15);
  xor xor_24 (xor_24_out, InputA16, InputB16);
  and and_26 (and_26_out, InputA16, InputB16);
  PullDown pulldown_5 (.out(diodeforward_4_out));
  Multiplexer #(.Bits(16)) multiplexer_6 (.sel(Clear), .in_0(ALU_B), .in_1({16{1'b0}}), .out(multiplexer_6_out));
  DiodeForward diodeforward_5 (.in(delay_4_out), .out(diodeforward_5_out));
  xor xor_25 (Output_9_16[0], Carry8, xor_17_out);
  xor xor_26 (Output_9_16[1], Carry9, xor_18_out);
  xor xor_27 (Output_9_16[2], Carry10, xor_19_out);
  xor xor_28 (Output_9_16[3], Carry11, xor_20_out);
  xor xor_29 (Output_9_16[4], Carry12, xor_21_out);
  xor xor_30 (Output_9_16[5], Carry13, xor_22_out);
  xor xor_31 (Output_9_16[6], Carry14, xor_23_out);
  xor xor_32 (Output_9_16[7], Carry15, xor_24_out);
  Multiplexer #(.Bits(16)) multiplexer_7 (.sel(Clear), .in_0(T1), .in_1({16{1'b0}}), .out(multiplexer_7_out));
  DiodeForward diodeforward_6 (.in(Clear), .out(diodeforward_4_out));
  Delay delay_5 (.in(diodeforward_4_out), .out(delay_5_out));
  Delay #(.delayTime(10)) delay_6 (.in(Clear), .out(delay_6_out));
  PullDown pulldown_6 (.out(diodeforward_5_out));
  and and_27 (and_27_out, xor_17_out, Carry8);
  and and_28 (and_28_out, xor_18_out, Carry9);
  and and_29 (and_29_out, xor_19_out, Carry10);
  and and_30 (and_30_out, xor_20_out, Carry11);
  and and_31 (and_31_out, xor_21_out, Carry12);
  and and_32 (and_32_out, xor_22_out, Carry13);
  and and_33 (and_33_out, xor_23_out, Carry14);
  and and_34 (and_34_out, xor_24_out, Carry15);
  Register #(.Bits(16)) Reg_A (.D(multiplexer_7_out), .C(delay_5_out), .en(Cycle_1), .Q(out_1));
  DiodeForward diodeforward_7 (.in(delay_6_out), .out(diodeforward_5_out));
  Register #(.Bits(16)) Reg_B (.D(multiplexer_6_out), .C(diodeforward_5_out), .en(Cycle_1), .Q(out_2));
  or or_12 (Carry9, and_19_out, and_27_out);
  or or_13 (Carry10, and_20_out, and_28_out);
  or or_14 (Carry11, and_21_out, and_29_out);
  or or_15 (Carry12, and_22_out, and_30_out);
  or or_16 (Carry13, and_23_out, and_31_out);
  or or_17 (Carry14, and_24_out, and_32_out);
  or or_18 (Carry15, and_25_out, and_33_out);
  or or_19 (or_19_out, and_26_out, and_34_out);
  Delay #(.delayTime(10)) delay_7 (.in(Cycle_1), .out(Cycle_3));

  // Other names for the same wires on the sheet: A[15:0] = out_1; Inverter[15:0] = out_1; Reg_A_Out[15:0] = out_1;
  //   Reg_cycle = Cycle_1; B[15:0] = out_2; Reg_B_Out[15:0] = out_2; Sub_OP[15:0] = out_2
endmodule
