// Digital circuit ALU.dig as structural Verilog
module ALU (
  input  [4:0] Keypad_Input,
  output [15:0] Output
);

  wire _16bitadder_1_p1, _16bitadder_1_p6, mutllplier10bit16_1_p2;
  wire [15:0] A_q, B_q;

  // _16Bit_decode_5bit _16bit_decode_5bit_1: pin names not known; wires that end beside it: Keypad_Input
  // _16bit_Calc_Plus_Decode _16bit_calc_plus_decode_1: pin names not known; wires that end beside it: Keypad_Input
  // _16bit_Calc_Subtract_Decode _16bit_calc_subtract_decode_1: pin names not known; wires that end beside it: Keypad_Input
  // _16bit_Calc_Equals _16bit_calc_equals_1: pin names not known; wires that end beside it: Keypad_Input
  Register #(.Bits(16)) A (.Q(A_q));  // open: D, C, en
  Register #(.Bits(16)) B (.Q(B_q));  // open: D, C, en
  // Mutllplier10Bit16 mutllplier10bit16_1: pin names not known; wires that end beside it: A_q, mutllplier10bit16_1_p2
  // _16BitAdder _16bitadder_1: pin names not known; wires that end beside it: _16bitadder_1_p1, _16bitadder_1_p1, mutllplier10bit16_1_p2, Output, Output, _16bitadder_1_p6
  // _16BitAdder _16bitadder_2: pin names not known; wires that end beside it: A_q, B_q, _16bitadder_1_p6, _16bitadder_1_p6

  // Notes on the sheet:
  //   BIN
  //   SUB
  //   ADD
  //   Equal
endmodule
