// Digital circuit AddSubCalculator.dig as structural Verilog
module AddSubCalculator (
  input  Clock,
  input  in_5,
  input  in_6,
  input  in_7,
  input  in_8,
  input  in_9,
  input  in_10,
  input  in_11,
  input  in_12,
  output [4:0] out_2,
  output [15:0] out_3,
  output [15:0] out_4
);

  wire _0, _1, _2, _3, _4, _5, _6, _7, _8, _9, _16bit_kmap_display_1_r, _16bit_kmap_display_1_s,
       _16bit_kmap_display_1_t, _16bit_kmap_display_1_u, _16bit_kmap_display_1_v, _16bit_kmap_display_1_w,
       _16bit_kmap_display_1_x, _16bit_kmap_display_1_y, _16bit_kmap_display_2_p2, _16bit_kmap_display_2_p3,
       _16bit_kmap_display_2_p4, _16bit_kmap_display_2_p5, _16bit_kmap_display_2_p6,
       _16bit_kmap_display_2_p7, _16bit_kmap_display_2_p8, _16bit_kmap_display_2_p9, bcd_16_bit_1_negative,
       button_1_out, C1, C3, C4, C5, C6, C8, C10, C14, CLR, cycle_input_5bit_1_cycle_out, eq, or_1_out,
       or_2_out, or_3_out, plus, rs_ff_as_1_q, tunnel;
  wire [3:0] bcd_16_bit_1_hundreds, bcd_16_bit_1_ones, bcd_16_bit_1_tens, bcd_16_bit_1_tens_of_thousands,
       bcd_16_bit_1_thousands;
  wire [4:0] diodeforward_2_out;
  wire [15:0] C2, C7, C9, C11, multiplexer_1_out, multiplexer_2_out;

  DiodeForward diodeforward_1 (.in(eq), .out(diodeforward_2_out[3]));
  DiodeForward diodeforward_2 (.in(eq), .out(diodeforward_2_out[4]));
  DiodeForward diodeforward_3 (.in(plus), .out(diodeforward_2_out[4]));
  DiodeForward diodeforward_4 (.in(tunnel), .out(diodeforward_2_out[4]));
  DiodeForward diodeforward_5 (.in(tunnel), .out(diodeforward_2_out[2]));
  DiodeForward diodeforward_6 (.in(CLR), .out(diodeforward_2_out[4]));
  DiodeForward diodeforward_7 (.in(CLR), .out(diodeforward_2_out[3]));
  DiodeForward diodeforward_8 (.in(CLR), .out(diodeforward_2_out[2]));
  PullDown pulldown_1 (.out(diodeforward_2_out[3]));
  PullDown pulldown_2 (.out(diodeforward_2_out[2]));
  PullDown pulldown_3 (.out(diodeforward_2_out[1]));
  PullDown pulldown_4 (.out(diodeforward_2_out[4]));
  Button button_1 (.out(button_1_out));
  PullDown pulldown_5 (.out(Clock));
  PullDown pulldown_6 (.out(diodeforward_2_out[0]));
  DiodeForward diodeforward_9 (.in(_1), .out(diodeforward_2_out[0]));
  DiodeForward diodeforward_10 (.in(_2), .out(diodeforward_2_out[1]));
  DiodeForward diodeforward_11 (.in(_3), .out(diodeforward_2_out[0]));
  DiodeForward diodeforward_12 (.in(_3), .out(diodeforward_2_out[1]));
  DiodeForward diodeforward_13 (.in(_4), .out(diodeforward_2_out[2]));
  DiodeForward diodeforward_14 (.in(_5), .out(diodeforward_2_out[0]));
  DiodeForward diodeforward_15 (.in(_5), .out(diodeforward_2_out[2]));
  DiodeForward diodeforward_16 (.in(_6), .out(diodeforward_2_out[1]));
  DiodeForward diodeforward_17 (.in(_6), .out(diodeforward_2_out[2]));
  DiodeForward diodeforward_18 (.in(_8), .out(diodeforward_2_out[3]));
  DiodeForward diodeforward_19 (.in(_0), .out(diodeforward_2_out[1]));
  DiodeForward diodeforward_20 (.in(_0), .out(diodeforward_2_out[3]));
  Cycle_Input_5Bit cycle_input_5bit_1 (
    .Keypad_In(diodeforward_2_out), .EC_I(button_1_out), .Cycle_Clock(Clock), .To_Decode(out_2),
    .Cycle_Out(cycle_input_5bit_1_cycle_out));
  _16bit_Key_Cycle _16bit_key_cycle_1 (.Binary(C2), .Cycle_In(C1), .Reg_A_IN(out_4), .Reg_A_OUT(C7), .Cycle_OUT(C8));
  DiodeForward diodeforward_21 (.in(_7), .out(diodeforward_2_out[0]));
  DiodeForward diodeforward_22 (.in(_7), .out(diodeforward_2_out[1]));
  DiodeForward diodeforward_23 (.in(_7), .out(diodeforward_2_out[2]));
  DiodeForward diodeforward_24 (.in(_9), .out(diodeforward_2_out[0]));
  DiodeForward diodeforward_25 (.in(_9), .out(diodeforward_2_out[3]));
  Seven_Seg seven_seg_1 (.a(in_5), .b(in_6), .c(in_7), .d(in_8), .e(in_12), .f(in_11), .g(in_10), .dp(in_9));
  PullDown pulldown_7 (.out(cycle_input_5bit_1_cycle_out));
  Decode_ALU_16Bit decode_alu_16bit_1 (
    .Decode_Key(out_2), .Cycle_In(cycle_input_5bit_1_cycle_out), .Cycle_Out(C1), .Binary(C2), .Subtract(C3),
    .Add(C4), .CLEAR(C5), .Equals(C6));
  Button u__7 (.out(_7));
  Button u__4 (.out(_4));
  Button u__1 (.out(_1));
  or or_1 (or_1_out, C8, C10);
  or or_2 (or_2_out, C3, C4);
  or or_3 (or_3_out, CLR, plus, tunnel);
  Button u__8 (.out(_8));
  Button u__5 (.out(_5));
  Button u__2 (.out(_2));
  Button u__0 (.out(_0));
  Multiplexer #(.Bits(16)) multiplexer_1 (.sel(or_2_out), .in_0(C7), .in_1(C11), .out(multiplexer_1_out));
  Multiplexer #(.Bits(16)) multiplexer_2 (.sel(rs_ff_as_1_q), .in_0(out_4), .in_1(C9), .out(multiplexer_2_out));
  RS_FF_AS rs_ff_as_1 (.S(eq), .R(or_3_out), .Q(rs_ff_as_1_q));  // open: nQ
  _16bit_Calc_Register_A_and_B _16bit_calc_register_a_and_b_1 (
    .Cycle_In(C1), .Reg_A_Cycle(or_1_out), .Reg_B_Cycle(C10), .Reg_A_Binary(multiplexer_1_out),
    .Reg_B_Binary(C9), .Reg_A_OUT(out_4), .Reg_B_OUT(out_3), .Cycle_Out(C14));  // open: Clear
  _16bit_Calc_ALU _16bit_calc_alu_1 (
    .Add(C4), .Sub(C3), .Reg_A(out_4), .Reg_B(out_3), .Cycle_In(C1), .Clear(C5), .Reg_B_OUT(C9),
    .Cycle_Out(C10), .Reg_A_OUT(C11));
  BCD_16_bit bcd_16_bit_1 (
    .Input(multiplexer_2_out), .Ones(bcd_16_bit_1_ones), .Tens(bcd_16_bit_1_tens),
    .Hundreds(bcd_16_bit_1_hundreds), .Thousands(bcd_16_bit_1_thousands),
    .Tens_of_Thousands(bcd_16_bit_1_tens_of_thousands), .Negative(bcd_16_bit_1_negative));  // open: Hundreds_of_Thousands
  Button u__9 (.out(_9));
  Button u__6 (.out(_6));
  Button u__3 (.out(_3));
  Button u_plus (.out(plus));
  Button button_2 (.out(tunnel));
  Button u_eq (.out(eq));
  Button u_CLR (.out(CLR));
  _16bit_KMAP_display _16bit_kmap_display_1 (
    .In(bcd_16_bit_1_ones), .Y(_16bit_kmap_display_1_y), .X(_16bit_kmap_display_1_x),
    .W(_16bit_kmap_display_1_w), .V(_16bit_kmap_display_1_v), .U(_16bit_kmap_display_1_u),
    .T(_16bit_kmap_display_1_t), .S(_16bit_kmap_display_1_s), .R(_16bit_kmap_display_1_r));
  // _16bit_KMAP_display _16bit_kmap_display_2: pin names not known; wires that end beside it: bcd_16_bit_1_tens, _16bit_kmap_display_2_p2, _16bit_kmap_display_2_p3, _16bit_kmap_display_2_p4, _16bit_kmap_display_2_p5, _16bit_kmap_display_2_p6, _16bit_kmap_display_2_p7, _16bit_kmap_display_2_p8, _16bit_kmap_display_2_p9
  // _16bit_KMAP_display _16bit_kmap_display_3: pin names not known; wires that end beside it: bcd_16_bit_1_hundreds
  // _16bit_KMAP_display _16bit_kmap_display_4: pin names not known; wires that end beside it: bcd_16_bit_1_thousands
  // _16bit_KMAP_display _16bit_kmap_display_5: pin names not known; wires that end beside it: bcd_16_bit_1_tens_of_thousands, bcd_16_bit_1_negative
  Seven_Seg seven_seg_2 (
    .a(_16bit_kmap_display_1_y), .b(_16bit_kmap_display_1_x), .c(_16bit_kmap_display_1_w),
    .d(_16bit_kmap_display_1_v), .e(_16bit_kmap_display_1_u), .f(_16bit_kmap_display_1_t),
    .g(_16bit_kmap_display_1_s), .dp(_16bit_kmap_display_1_r));
  Seven_Seg seven_seg_3 (
    .a(_16bit_kmap_display_2_p2), .b(_16bit_kmap_display_2_p3), .c(_16bit_kmap_display_2_p4),
    .d(_16bit_kmap_display_2_p5), .e(_16bit_kmap_display_2_p6), .f(_16bit_kmap_display_2_p7),
    .g(_16bit_kmap_display_2_p8), .dp(_16bit_kmap_display_2_p9));

  // Other names for the same wires on the sheet: C12[15:0] = out_4; C13[15:0] = out_3; CLK = Clock

  // Notes on the sheet:
  //   Clock: Hz: 1000
  //   0000 0000 = OFF
  //   1111 1100 = 0
  //   0110 0000 = 1
  //   1101 1010 = 2
  //   1111 0010 = 3
  //   0110 0110 = 4
  //   1011 0110 = 5
  //   1011 1110 = 6
  //   1110 0000 = 7
  //   1111 1110 = 8
  //   1110 0110 = 9
  //   00001 - 1
  //   00010 - 2
  //   00011 - 3
  //   00100 - 4
  //   00101 - 5
  //   00110 - 6
  //   00111 - 7
  //   01000 - 8
  //   01001 - 9
  //   01010 - 0
  //   11000 - =
  //   10000 - +
  //   10100 - -
  //   11100 - CLR
  //   1 bit = 0 - 1
  //   2 bit = 0 - 3
  //   3 bit = 0 - 8 
  //   2^n = bit
  //   2 4 8 16 32 
  //   5bit = 0 - 16 | -9 - 7
  //   6bit = 0 - 32 | -17 - 15
endmodule
