// Digital circuit Adder non-abstract.dig as structural Verilog
module Adder_non_abstract (
  input  [15:0] A,
  input  [15:0] B,
  output [15:0] Sum
);

  wire and_1_out, and_2_out, and_3_out, and_4_out, and_5_out, and_6_out, and_7_out, and_8_out, and_9_out,
       and_10_out, and_11_out, and_12_out, and_13_out, and_14_out, and_15_out, and_16_out, and_17_out,
       and_18_out, and_19_out, and_20_out, and_21_out, and_22_out, and_23_out, and_24_out, and_25_out,
       and_26_out, and_27_out, and_28_out, and_29_out, and_30_out, and_31_out, and_32_out, Carry1, Carry2,
       Carry3, Carry4, Carry5, Carry6, Carry7, Carry8, Carry9, Carry10, Carry11, Carry12, Carry13, Carry14,
       Carry15, or_16_out, xor_1_out, xor_2_out, xor_3_out, xor_4_out, xor_5_out, xor_6_out, xor_7_out,
       xor_8_out, xor_17_out, xor_18_out, xor_19_out, xor_20_out, xor_21_out, xor_22_out, xor_23_out,
       xor_24_out;

  xor xor_1 (xor_1_out, A[0], B[0]);
  and and_1 (and_1_out, A[0], B[0]);
  xor xor_2 (xor_2_out, A[1], B[1]);
  and and_2 (and_2_out, A[1], B[1]);
  xor xor_3 (xor_3_out, A[2], B[2]);
  and and_3 (and_3_out, A[2], B[2]);
  xor xor_4 (xor_4_out, A[3], B[3]);
  and and_4 (and_4_out, A[3], B[3]);
  xor xor_5 (xor_5_out, A[4], B[4]);
  and and_5 (and_5_out, A[4], B[4]);
  xor xor_6 (xor_6_out, A[5], B[5]);
  and and_6 (and_6_out, A[5], B[5]);
  xor xor_7 (xor_7_out, A[6], B[6]);
  and and_7 (and_7_out, A[6], B[6]);
  xor xor_8 (xor_8_out, A[7], B[7]);
  and and_8 (and_8_out, A[7], B[7]);
  xor xor_9 (Sum[0], 1'b0, xor_1_out);
  and and_9 (and_9_out, xor_1_out, 1'b0);
  xor xor_10 (Sum[1], Carry1, xor_2_out);
  and and_10 (and_10_out, xor_2_out, Carry1);
  xor xor_11 (Sum[2], Carry2, xor_3_out);
  and and_11 (and_11_out, xor_3_out, Carry2);
  xor xor_12 (Sum[3], Carry3, xor_4_out);
  and and_12 (and_12_out, xor_4_out, Carry3);
  xor xor_13 (Sum[4], Carry4, xor_5_out);
  and and_13 (and_13_out, xor_5_out, Carry4);
  xor xor_14 (Sum[5], Carry5, xor_6_out);
  and and_14 (and_14_out, xor_6_out, Carry5);
  xor xor_15 (Sum[6], Carry6, xor_7_out);
  and and_15 (and_15_out, xor_7_out, Carry6);
  xor xor_16 (Sum[7], Carry7, xor_8_out);
  and and_16 (and_16_out, xor_8_out, Carry7);
  or or_1 (Carry1, and_1_out, and_9_out);
  or or_2 (Carry2, and_2_out, and_10_out);
  or or_3 (Carry3, and_3_out, and_11_out);
  or or_4 (Carry4, and_4_out, and_12_out);
  or or_5 (Carry5, and_5_out, and_13_out);
  or or_6 (Carry6, and_6_out, and_14_out);
  or or_7 (Carry7, and_7_out, and_15_out);
  or or_8 (Carry8, and_8_out, and_16_out);
  xor xor_17 (xor_17_out, A[8], B[8]);
  xor xor_18 (xor_18_out, A[9], B[9]);
  xor xor_19 (xor_19_out, A[10], B[10]);
  xor xor_20 (xor_20_out, A[11], B[11]);
  xor xor_21 (xor_21_out, A[12], B[12]);
  xor xor_22 (xor_22_out, A[13], B[13]);
  xor xor_23 (xor_23_out, A[14], B[14]);
  xor xor_24 (xor_24_out, A[15], B[15]);
  and and_17 (and_17_out, A[8], B[8]);
  and and_18 (and_18_out, A[9], B[9]);
  and and_19 (and_19_out, A[10], B[10]);
  and and_20 (and_20_out, A[11], B[11]);
  and and_21 (and_21_out, A[12], B[12]);
  and and_22 (and_22_out, A[13], B[13]);
  and and_23 (and_23_out, A[14], B[14]);
  and and_24 (and_24_out, A[15], B[15]);
  xor xor_25 (Sum[8], Carry8, xor_17_out);
  and and_25 (and_25_out, xor_17_out, Carry8);
  xor xor_26 (Sum[9], Carry9, xor_18_out);
  and and_26 (and_26_out, xor_18_out, Carry9);
  xor xor_27 (Sum[10], Carry10, xor_19_out);
  and and_27 (and_27_out, xor_19_out, Carry10);
  xor xor_28 (Sum[11], Carry11, xor_20_out);
  and and_28 (and_28_out, xor_20_out, Carry11);
  xor xor_29 (Sum[12], Carry12, xor_21_out);
  and and_29 (and_29_out, xor_21_out, Carry12);
  xor xor_30 (Sum[13], Carry13, xor_22_out);
  and and_30 (and_30_out, xor_22_out, Carry13);
  xor xor_31 (Sum[14], Carry14, xor_23_out);
  and and_31 (and_31_out, xor_23_out, Carry14);
  xor xor_32 (Sum[15], Carry15, xor_24_out);
  and and_32 (and_32_out, xor_24_out, Carry15);
  or or_9 (Carry9, and_17_out, and_25_out);
  or or_10 (Carry10, and_18_out, and_26_out);
  or or_11 (Carry11, and_19_out, and_27_out);
  or or_12 (Carry12, and_20_out, and_28_out);
  or or_13 (Carry13, and_21_out, and_29_out);
  or or_14 (Carry14, and_22_out, and_30_out);
  or or_15 (Carry15, and_23_out, and_31_out);
  or or_16 (or_16_out, and_24_out, and_32_out);
  // also tied to GND on the sheet: or_16_out

  // Other names for the same wires on the sheet: Output_9_16[7:0] = Sum[15:8]; InputA1 = A[0]; InputA2 = A[1];
  //   InputA3 = A[2]; InputA4 = A[3]; InputA5 = A[4]; InputA6 = A[5]; InputA7 = A[6]; InputA8 = A[7]; InputA9 = A[8];
  //   InputA10 = A[9]; InputA11 = A[10]; InputA12 = A[11]; InputA13 = A[12]; InputA14 = A[13]; InputA15 = A[14];
  //   InputA16 = A[15]; InputB1 = B[0]; InputB2 = B[1]; InputB3 = B[2]; InputB4 = B[3]; InputB5 = B[4];
  //   InputB6 = B[5]; InputB7 = B[6]; InputB8 = B[7]; InputB9 = B[8]; InputB10 = B[9]; InputB11 = B[10];
  //   InputB12 = B[11]; InputB13 = B[12]; InputB14 = B[13]; InputB15 = B[14]; InputB16 = B[15]

  // Notes on the sheet:
  //   A: Secondary input for adding 2 integers
  //   B: Secondary input for adding 2 integers
  //   Sum: Product of 2 integers
endmodule
