// Digital circuit BCD 16 bit.dig as structural Verilog
module BCD_16_bit (
  input  [15:0] Input,
  output [3:0] Ones,
  output [3:0] Tens,
  output [3:0] Hundreds,
  output [3:0] Thousands,
  output [3:0] Tens_of_Thousands,
  output [3:0] Hundreds_of_Thousands,
  output Negative
);

  wire bcd_gate_1_o_1, bcd_gate_1_o_2, bcd_gate_1_o_3, bcd_gate_1_o_4, bcd_gate_2_o_1, bcd_gate_2_o_2,
       bcd_gate_2_o_3, bcd_gate_2_o_4, bcd_gate_3_o_1, bcd_gate_3_o_2, bcd_gate_3_o_3, bcd_gate_3_o_4,
       bcd_gate_4_o_1, bcd_gate_4_o_2, bcd_gate_4_o_3, bcd_gate_4_o_4, bcd_gate_5_o_1, bcd_gate_5_o_2,
       bcd_gate_5_o_3, bcd_gate_5_o_4, bcd_gate_6_o_1, bcd_gate_6_o_2, bcd_gate_6_o_3, bcd_gate_6_o_4,
       bcd_gate_7_o_1, bcd_gate_7_o_2, bcd_gate_7_o_3, bcd_gate_7_o_4, bcd_gate_8_o_1, bcd_gate_8_o_2,
       bcd_gate_8_o_3, bcd_gate_8_o_4, bcd_gate_9_o_1, bcd_gate_9_o_2, bcd_gate_9_o_3, bcd_gate_9_o_4,
       bcd_gate_10_o_1, bcd_gate_10_o_2, bcd_gate_10_o_3, bcd_gate_10_o_4, bcd_gate_11_o_1, bcd_gate_11_o_2,
       bcd_gate_11_o_3, bcd_gate_11_o_4, bcd_gate_12_o_1, bcd_gate_12_o_2, bcd_gate_12_o_3, bcd_gate_12_o_4,
       bcd_gate_13_o_1, bcd_gate_13_o_2, bcd_gate_13_o_3, bcd_gate_13_o_4, bcd_gate_14_o_1, bcd_gate_14_o_2,
       bcd_gate_14_o_3, bcd_gate_14_o_4, bcd_gate_15_o_1, bcd_gate_15_o_2, bcd_gate_15_o_3, bcd_gate_15_o_4,
       bcd_gate_16_o_1, bcd_gate_16_o_2, bcd_gate_16_o_3, bcd_gate_16_o_4, bcd_gate_17_o_1, bcd_gate_17_o_2,
       bcd_gate_17_o_3, bcd_gate_17_o_4, bcd_gate_18_o_1, bcd_gate_18_o_2, bcd_gate_18_o_3, bcd_gate_18_o_4,
       bcd_gate_19_o_1, bcd_gate_19_o_2, bcd_gate_19_o_3, bcd_gate_19_o_4, bcd_gate_20_o_1, bcd_gate_20_o_2,
       bcd_gate_20_o_3, bcd_gate_20_o_4, bcd_gate_21_o_1, bcd_gate_21_o_2, bcd_gate_21_o_3, bcd_gate_21_o_4,
       bcd_gate_22_o_1, bcd_gate_22_o_2, bcd_gate_22_o_3, bcd_gate_22_o_4, bcd_gate_23_o_1, bcd_gate_23_o_2,
       bcd_gate_23_o_3, bcd_gate_23_o_4, bcd_gate_24_o_1, bcd_gate_24_o_2, bcd_gate_24_o_3, bcd_gate_24_o_4,
       bcd_gate_25_o_1, bcd_gate_25_o_2, bcd_gate_25_o_3, bcd_gate_25_o_4, bcd_gate_26_o_1, bcd_gate_26_o_2,
       bcd_gate_26_o_3, bcd_gate_26_o_4, bcd_gate_27_o_1, bcd_gate_27_o_2, bcd_gate_27_o_3, bcd_gate_27_o_4,
       bcd_gate_28_o_1, bcd_gate_28_o_2, bcd_gate_28_o_3, bcd_gate_28_o_4, bcd_gate_29_o_1, bcd_gate_29_o_2,
       bcd_gate_29_o_3, bcd_gate_29_o_4, bcd_gate_30_o_1, bcd_gate_30_o_2, bcd_gate_30_o_3, bcd_gate_30_o_4,
       bcd_gate_31_o_1, bcd_gate_31_o_2, bcd_gate_31_o_3, bcd_gate_31_o_4, bcd_gate_32_o_1, bcd_gate_32_o_2,
       bcd_gate_32_o_3, bcd_gate_32_o_4, bcd_gate_33_o_1, bcd_gate_33_o_2, bcd_gate_33_o_3, bcd_gate_33_o_4,
       bcd_gate_34_o_1, bcd_gate_34_o_2, bcd_gate_34_o_3, bcd_gate_34_o_4, bcd_gate_35_o_1, bcd_gate_35_o_2,
       bcd_gate_35_o_3, bcd_gate_35_o_4, pulldown_1_out, pulldown_2_out, pulldown_3_out, pulldown_4_out,
       pulldown_5_out, pulldown_6_out, pulldown_7_out, pulldown_8_out, pulldown_9_out;
  wire [15:0] _16bitinverter_1_o;
  wire [15:1] multiplexer_1_out;

  _16BitInverter _16bitinverter_1 (.I(Input), .O(_16bitinverter_1_o));
  Multiplexer #(.Bits(16)) multiplexer_1 (
    .sel(Input[15]), .in_0(Input), .in_1(_16bitinverter_1_o), .out({multiplexer_1_out, Ones[0]}));
  BCD_Gate bcd_gate_1 (
    .B_1(multiplexer_1_out[14]), .B_2(multiplexer_1_out[15]), .B_3(pulldown_1_out), .B_4(pulldown_2_out),
    .O_1(bcd_gate_1_o_1), .O_2(bcd_gate_1_o_2), .O_3(bcd_gate_1_o_3), .O_4(bcd_gate_1_o_4));
  PullDown pulldown_1 (.out(pulldown_1_out));
  PullDown pulldown_2 (.out(pulldown_2_out));
  PullDown pulldown_3 (.out(pulldown_3_out));
  PullDown pulldown_4 (.out(pulldown_4_out));
  PullDown pulldown_5 (.out(pulldown_5_out));
  PullDown pulldown_6 (.out(pulldown_6_out));
  PullDown pulldown_7 (.out(pulldown_7_out));
  PullDown pulldown_8 (.out(pulldown_8_out));
  PullDown pulldown_9 (.out(pulldown_9_out));
  BCD_Gate bcd_gate_2 (
    .B_1(multiplexer_1_out[13]), .B_2(bcd_gate_1_o_1), .B_3(bcd_gate_1_o_2), .B_4(bcd_gate_1_o_3),
    .O_1(bcd_gate_2_o_1), .O_2(bcd_gate_2_o_2), .O_3(bcd_gate_2_o_3), .O_4(bcd_gate_2_o_4));
  BCD_Gate bcd_gate_3 (
    .B_1(multiplexer_1_out[12]), .B_2(bcd_gate_2_o_1), .B_3(bcd_gate_2_o_2), .B_4(bcd_gate_2_o_3),
    .O_1(bcd_gate_3_o_1), .O_2(bcd_gate_3_o_2), .O_3(bcd_gate_3_o_3), .O_4(bcd_gate_3_o_4));
  BCD_Gate bcd_gate_4 (
    .B_1(multiplexer_1_out[11]), .B_2(bcd_gate_3_o_1), .B_3(bcd_gate_3_o_2), .B_4(bcd_gate_3_o_3),
    .O_1(bcd_gate_4_o_1), .O_2(bcd_gate_4_o_2), .O_3(bcd_gate_4_o_3), .O_4(bcd_gate_4_o_4));
  BCD_Gate bcd_gate_5 (
    .B_1(bcd_gate_3_o_4), .B_2(bcd_gate_2_o_4), .B_3(bcd_gate_1_o_4), .B_4(pulldown_3_out),
    .O_1(bcd_gate_5_o_1), .O_2(bcd_gate_5_o_2), .O_3(bcd_gate_5_o_3), .O_4(bcd_gate_5_o_4));
  BCD_Gate bcd_gate_6 (
    .B_1(multiplexer_1_out[10]), .B_2(bcd_gate_4_o_1), .B_3(bcd_gate_4_o_2), .B_4(bcd_gate_4_o_3),
    .O_1(bcd_gate_6_o_1), .O_2(bcd_gate_6_o_2), .O_3(bcd_gate_6_o_3), .O_4(bcd_gate_6_o_4));
  BCD_Gate bcd_gate_7 (
    .B_1(bcd_gate_4_o_4), .B_2(bcd_gate_5_o_1), .B_3(bcd_gate_5_o_2), .B_4(bcd_gate_5_o_3),
    .O_1(bcd_gate_7_o_1), .O_2(bcd_gate_7_o_2), .O_3(bcd_gate_7_o_3), .O_4(bcd_gate_7_o_4));
  BCD_Gate bcd_gate_8 (
    .B_1(multiplexer_1_out[9]), .B_2(bcd_gate_6_o_1), .B_3(bcd_gate_6_o_2), .B_4(bcd_gate_6_o_3),
    .O_1(bcd_gate_8_o_1), .O_2(bcd_gate_8_o_2), .O_3(bcd_gate_8_o_3), .O_4(bcd_gate_8_o_4));
  BCD_Gate bcd_gate_9 (
    .B_1(bcd_gate_6_o_4), .B_2(bcd_gate_7_o_1), .B_3(bcd_gate_7_o_2), .B_4(bcd_gate_7_o_3),
    .O_1(bcd_gate_9_o_1), .O_2(bcd_gate_9_o_2), .O_3(bcd_gate_9_o_3), .O_4(bcd_gate_9_o_4));
  BCD_Gate bcd_gate_10 (
    .B_1(multiplexer_1_out[8]), .B_2(bcd_gate_8_o_1), .B_3(bcd_gate_8_o_2), .B_4(bcd_gate_8_o_3),
    .O_1(bcd_gate_10_o_1), .O_2(bcd_gate_10_o_2), .O_3(bcd_gate_10_o_3), .O_4(bcd_gate_10_o_4));
  BCD_Gate bcd_gate_11 (
    .B_1(bcd_gate_8_o_4), .B_2(bcd_gate_9_o_1), .B_3(bcd_gate_9_o_2), .B_4(bcd_gate_9_o_3),
    .O_1(bcd_gate_11_o_1), .O_2(bcd_gate_11_o_2), .O_3(bcd_gate_11_o_3), .O_4(bcd_gate_11_o_4));
  BCD_Gate bcd_gate_12 (
    .B_1(bcd_gate_9_o_4), .B_2(bcd_gate_7_o_4), .B_3(bcd_gate_5_o_4), .B_4(pulldown_4_out),
    .O_1(bcd_gate_12_o_1), .O_2(bcd_gate_12_o_2), .O_3(bcd_gate_12_o_3), .O_4(bcd_gate_12_o_4));
  BCD_Gate bcd_gate_13 (
    .B_1(multiplexer_1_out[7]), .B_2(bcd_gate_10_o_1), .B_3(bcd_gate_10_o_2), .B_4(bcd_gate_10_o_3),
    .O_1(bcd_gate_13_o_1), .O_2(bcd_gate_13_o_2), .O_3(bcd_gate_13_o_3), .O_4(bcd_gate_13_o_4));
  BCD_Gate bcd_gate_14 (
    .B_1(bcd_gate_10_o_4), .B_2(bcd_gate_11_o_1), .B_3(bcd_gate_11_o_2), .B_4(bcd_gate_11_o_3),
    .O_1(bcd_gate_14_o_1), .O_2(bcd_gate_14_o_2), .O_3(bcd_gate_14_o_3), .O_4(bcd_gate_14_o_4));
  BCD_Gate bcd_gate_15 (
    .B_1(bcd_gate_11_o_4), .B_2(bcd_gate_12_o_1), .B_3(bcd_gate_12_o_2), .B_4(bcd_gate_12_o_3),
    .O_1(bcd_gate_15_o_1), .O_2(bcd_gate_15_o_2), .O_3(bcd_gate_15_o_3), .O_4(bcd_gate_15_o_4));
  BCD_Gate bcd_gate_16 (
    .B_1(multiplexer_1_out[6]), .B_2(bcd_gate_13_o_1), .B_3(bcd_gate_13_o_2), .B_4(bcd_gate_13_o_3),
    .O_1(bcd_gate_16_o_1), .O_2(bcd_gate_16_o_2), .O_3(bcd_gate_16_o_3), .O_4(bcd_gate_16_o_4));
  BCD_Gate bcd_gate_17 (
    .B_1(bcd_gate_13_o_4), .B_2(bcd_gate_14_o_1), .B_3(bcd_gate_14_o_2), .B_4(bcd_gate_14_o_3),
    .O_1(bcd_gate_17_o_1), .O_2(bcd_gate_17_o_2), .O_3(bcd_gate_17_o_3), .O_4(bcd_gate_17_o_4));
  BCD_Gate bcd_gate_18 (
    .B_1(bcd_gate_14_o_4), .B_2(bcd_gate_15_o_1), .B_3(bcd_gate_15_o_2), .B_4(bcd_gate_15_o_3),
    .O_1(bcd_gate_18_o_1), .O_2(bcd_gate_18_o_2), .O_3(bcd_gate_18_o_3), .O_4(bcd_gate_18_o_4));
  BCD_Gate bcd_gate_19 (
    .B_1(multiplexer_1_out[5]), .B_2(bcd_gate_16_o_1), .B_3(bcd_gate_16_o_2), .B_4(bcd_gate_16_o_3),
    .O_1(bcd_gate_19_o_1), .O_2(bcd_gate_19_o_2), .O_3(bcd_gate_19_o_3), .O_4(bcd_gate_19_o_4));
  BCD_Gate bcd_gate_20 (
    .B_1(bcd_gate_16_o_4), .B_2(bcd_gate_17_o_1), .B_3(bcd_gate_17_o_2), .B_4(bcd_gate_17_o_3),
    .O_1(bcd_gate_20_o_1), .O_2(bcd_gate_20_o_2), .O_3(bcd_gate_20_o_3), .O_4(bcd_gate_20_o_4));
  BCD_Gate bcd_gate_21 (
    .B_1(bcd_gate_17_o_4), .B_2(bcd_gate_18_o_1), .B_3(bcd_gate_18_o_2), .B_4(bcd_gate_18_o_3),
    .O_1(bcd_gate_21_o_1), .O_2(bcd_gate_21_o_2), .O_3(bcd_gate_21_o_3), .O_4(bcd_gate_21_o_4));
  BCD_Gate bcd_gate_22 (
    .B_1(bcd_gate_18_o_4), .B_2(bcd_gate_15_o_4), .B_3(bcd_gate_12_o_4), .B_4(pulldown_5_out),
    .O_1(bcd_gate_22_o_1), .O_2(bcd_gate_22_o_2), .O_3(bcd_gate_22_o_3), .O_4(bcd_gate_22_o_4));
  BCD_Gate bcd_gate_23 (
    .B_1(multiplexer_1_out[4]), .B_2(bcd_gate_19_o_1), .B_3(bcd_gate_19_o_2), .B_4(bcd_gate_19_o_3),
    .O_1(bcd_gate_23_o_1), .O_2(bcd_gate_23_o_2), .O_3(bcd_gate_23_o_3), .O_4(bcd_gate_23_o_4));
  BCD_Gate bcd_gate_24 (
    .B_1(bcd_gate_19_o_4), .B_2(bcd_gate_20_o_1), .B_3(bcd_gate_20_o_2), .B_4(bcd_gate_20_o_3),
    .O_1(bcd_gate_24_o_1), .O_2(bcd_gate_24_o_2), .O_3(bcd_gate_24_o_3), .O_4(bcd_gate_24_o_4));
  BCD_Gate bcd_gate_25 (
    .B_1(bcd_gate_20_o_4), .B_2(bcd_gate_21_o_1), .B_3(bcd_gate_21_o_2), .B_4(bcd_gate_21_o_3),
    .O_1(bcd_gate_25_o_1), .O_2(bcd_gate_25_o_2), .O_3(bcd_gate_25_o_3), .O_4(bcd_gate_25_o_4));
  BCD_Gate bcd_gate_26 (
    .B_1(bcd_gate_21_o_4), .B_2(bcd_gate_22_o_1), .B_3(bcd_gate_22_o_2), .B_4(bcd_gate_22_o_3),
    .O_1(bcd_gate_26_o_1), .O_2(bcd_gate_26_o_2), .O_3(bcd_gate_26_o_3), .O_4(bcd_gate_26_o_4));
  BCD_Gate bcd_gate_27 (
    .B_1(multiplexer_1_out[3]), .B_2(bcd_gate_23_o_1), .B_3(bcd_gate_23_o_2), .B_4(bcd_gate_23_o_3),
    .O_1(bcd_gate_27_o_1), .O_2(bcd_gate_27_o_2), .O_3(bcd_gate_27_o_3), .O_4(bcd_gate_27_o_4));
  BCD_Gate bcd_gate_28 (
    .B_1(bcd_gate_23_o_4), .B_2(bcd_gate_24_o_1), .B_3(bcd_gate_24_o_2), .B_4(bcd_gate_24_o_3),
    .O_1(bcd_gate_28_o_1), .O_2(bcd_gate_28_o_2), .O_3(bcd_gate_28_o_3), .O_4(bcd_gate_28_o_4));
  BCD_Gate bcd_gate_29 (
    .B_1(bcd_gate_24_o_4), .B_2(bcd_gate_25_o_1), .B_3(bcd_gate_25_o_2), .B_4(bcd_gate_25_o_3),
    .O_1(bcd_gate_29_o_1), .O_2(bcd_gate_29_o_2), .O_3(bcd_gate_29_o_3), .O_4(bcd_gate_29_o_4));
  BCD_Gate bcd_gate_30 (
    .B_1(bcd_gate_25_o_4), .B_2(bcd_gate_26_o_1), .B_3(bcd_gate_26_o_2), .B_4(bcd_gate_26_o_3),
    .O_1(bcd_gate_30_o_1), .O_2(bcd_gate_30_o_2), .O_3(bcd_gate_30_o_3), .O_4(bcd_gate_30_o_4));
  BCD_Gate bcd_gate_31 (
    .B_1(multiplexer_1_out[2]), .B_2(bcd_gate_27_o_1), .B_3(bcd_gate_27_o_2), .B_4(bcd_gate_27_o_3),
    .O_1(bcd_gate_31_o_1), .O_2(bcd_gate_31_o_2), .O_3(bcd_gate_31_o_3), .O_4(bcd_gate_31_o_4));
  BCD_Gate bcd_gate_32 (
    .B_1(bcd_gate_27_o_4), .B_2(bcd_gate_28_o_1), .B_3(bcd_gate_28_o_2), .B_4(bcd_gate_28_o_3),
    .O_1(bcd_gate_32_o_1), .O_2(bcd_gate_32_o_2), .O_3(bcd_gate_32_o_3), .O_4(bcd_gate_32_o_4));
  BCD_Gate bcd_gate_33 (
    .B_1(bcd_gate_28_o_4), .B_2(bcd_gate_29_o_1), .B_3(bcd_gate_29_o_2), .B_4(bcd_gate_29_o_3),
    .O_1(bcd_gate_33_o_1), .O_2(bcd_gate_33_o_2), .O_3(bcd_gate_33_o_3), .O_4(bcd_gate_33_o_4));
  BCD_Gate bcd_gate_34 (
    .B_1(bcd_gate_29_o_4), .B_2(bcd_gate_30_o_1), .B_3(bcd_gate_30_o_2), .B_4(bcd_gate_30_o_3),
    .O_1(bcd_gate_34_o_1), .O_2(bcd_gate_34_o_2), .O_3(bcd_gate_34_o_3), .O_4(bcd_gate_34_o_4));
  BCD_Gate bcd_gate_35 (
    .B_1(bcd_gate_30_o_4), .B_2(bcd_gate_26_o_4), .B_3(bcd_gate_22_o_4), .B_4(pulldown_6_out),
    .O_1(bcd_gate_35_o_1), .O_2(bcd_gate_35_o_2), .O_3(bcd_gate_35_o_3), .O_4(bcd_gate_35_o_4));
  BCD_Gate bcd_gate_36 (
    .B_1(multiplexer_1_out[1]), .B_2(bcd_gate_31_o_1), .B_3(bcd_gate_31_o_2), .B_4(bcd_gate_31_o_3),
    .O_1(Ones[1]), .O_2(Ones[2]), .O_3(Ones[3]), .O_4(Tens[0]));
  BCD_Gate bcd_gate_37 (
    .B_1(bcd_gate_31_o_4), .B_2(bcd_gate_32_o_1), .B_3(bcd_gate_32_o_2), .B_4(bcd_gate_32_o_3),
    .O_1(Tens[1]), .O_2(Tens[2]), .O_3(Tens[3]), .O_4(Hundreds[0]));
  BCD_Gate bcd_gate_38 (
    .B_1(bcd_gate_32_o_4), .B_2(bcd_gate_33_o_1), .B_3(bcd_gate_33_o_2), .B_4(bcd_gate_33_o_3),
    .O_1(Hundreds[1]), .O_2(Hundreds[2]), .O_3(Hundreds[3]), .O_4(Thousands[0]));
  BCD_Gate bcd_gate_39 (
    .B_1(bcd_gate_33_o_4), .B_2(bcd_gate_34_o_1), .B_3(bcd_gate_34_o_2), .B_4(bcd_gate_34_o_3),
    .O_1(Thousands[1]), .O_2(Thousands[2]), .O_3(Thousands[3]), .O_4(Tens_of_Thousands[0]));
  BCD_Gate bcd_gate_40 (
    .B_1(bcd_gate_34_o_4), .B_2(bcd_gate_35_o_1), .B_3(bcd_gate_35_o_2), .B_4(bcd_gate_35_o_3),
    .O_1(Tens_of_Thousands[1]), .O_2(Tens_of_Thousands[2]), .O_3(Tens_of_Thousands[3]),
    .O_4(Hundreds_of_Thousands[0]));
  BCD_Gate bcd_gate_41 (
    .B_1(bcd_gate_35_o_4), .B_2(pulldown_7_out), .B_3(pulldown_8_out), .B_4(pulldown_9_out),
    .O_1(Hundreds_of_Thousands[1]), .O_2(Hundreds_of_Thousands[2]), .O_3(Hundreds_of_Thousands[3]));  // open: O_4

  assign Negative = Input[15];
endmodule
