// Digital circuit BCD Gate.dig as structural Verilog
module BCD_Gate (
  input  B_1,
  input  B_2,
  input  B_3,
  input  B_4,
  output O_1,
  output O_2,
  output O_3,
  output O_4
);

  wire and_1_out, or_1_out, or_2_out;
  wire [3:0] pulldown_1_out, pulldown_2_out, pulldown_3_out;
  wire [15:0] _16bitadder_1_sum;

  PullDown #(.Bits(4)) pulldown_1 (.out(pulldown_1_out));
  PullDown #(.Bits(4)) pulldown_2 (.out(pulldown_2_out));
  PullDown #(.Bits(4)) pulldown_3 (.out(pulldown_3_out));
  or or_1 (or_1_out, B_1, B_2);
  and and_1 (and_1_out, or_1_out, B_3);
  _16BitAdder _16bitadder_1 (
    .A({pulldown_3_out, pulldown_2_out, pulldown_1_out, B_4, B_3, B_2, B_1}), .B(16'h3),
    .Sum(_16bitadder_1_sum));  // open: Of
  or or_2 (or_2_out, and_1_out, B_4);
  Multiplexer #(.Bits(4)) multiplexer_1 (
    .sel(or_2_out), .in_0({B_4, B_3, B_2, B_1}), .in_1(_16bitadder_1_sum[3:0]), .out({O_4, O_3, O_2, O_1}));
endmodule
