// Digital circuit Cycle-Input-5Bit.dig as structural Verilog
module Cycle_Input_5Bit (
  input  [4:0] Keypad_In,
  input  EC_I,
  input  Cycle_Clock,
  output [4:0] To_Decode,
  output Cycle_Out
);

  wire and_1_out, and_2_out, and_3_out, diodeforward_2_out, not_1_out, or_1_out, or_2_out, or_3_out,
       or_4_out, rs_ff_as_1_nq, rs_ff_as_1_q, rs_ff_as_2_nq, xor_1_out, xor_2_out;

  or or_1 (or_1_out, Keypad_In[0], Keypad_In[1]);
  or or_2 (or_2_out, or_1_out, Keypad_In[2]);
  or or_3 (or_3_out, or_2_out, Keypad_In[3]);
  or or_4 (or_4_out, or_3_out, Keypad_In[4]);
  not not_1 (not_1_out, or_4_out);
  and and_1 (and_1_out, not_1_out, Cycle_Out);
  xor xor_1 (xor_1_out, Cycle_Out, or_4_out);
  and and_2 (and_2_out, EC_I, not_1_out);
  xor xor_2 (xor_2_out, and_1_out, xor_1_out);
  and and_3 (and_3_out, Cycle_Clock, and_2_out);
  DiodeForward diodeforward_1 (.in(rs_ff_as_1_q), .out(Cycle_Out));
  RS_FF_AS rs_ff_as_1 (.S(xor_2_out), .R(Cycle_Out), .Q(rs_ff_as_1_q), .nQ(rs_ff_as_1_nq));
  DiodeForward diodeforward_2 (.in(Cycle_Out), .out(diodeforward_2_out));
  PullDown pulldown_1 (.out(Cycle_Out));
  RS_FF_AS rs_ff_as_2 (.S(rs_ff_as_1_q), .R(and_3_out), .Q(Cycle_Out), .nQ(rs_ff_as_2_nq));
  PullDown pulldown_2 (.out(rs_ff_as_1_nq));
  DiodeForward diodeforward_3 (.in(rs_ff_as_1_q), .out(diodeforward_2_out));
  PullDown pulldown_3 (.out(diodeforward_2_out));
  PullDown pulldown_4 (.out(diodeforward_2_out));
  DiodeForward diodeforward_4 (.in(and_3_out), .out(diodeforward_2_out));
  PullDown pulldown_5 (.out(rs_ff_as_2_nq));
  Register #(.Bits(5)) Cycle_Register (.D(Keypad_In), .C(diodeforward_2_out), .en(diodeforward_2_out), .Q(To_Decode));

  // Notes on the sheet:
  //   Cycle_Clock: Hz: 1000
endmodule
