// Digital circuit Decode-ALU-16Bit.dig as structural Verilog
module Decode_ALU_16Bit (
  input  [4:0] Decode_Key,
  input  Cycle_In,
  output Cycle_Out,
  output [15:0] Binary,
  output Subtract,
  output Add,
  output CLEAR,
  output Equals
);

  wire _4bit_or_1_out, _16_bit_5_bit_key_to_binary_1__0cycle, and_1_out, and_2_out, and_3_out, and_4_out,
       and_5_out, or_1_out;

  _16_bit_5_bit_Key_to_Binary _16_bit_5_bit_key_to_binary_1 (
    .I(Decode_Key), ._0Cycle(_16_bit_5_bit_key_to_binary_1__0cycle), .Binary_OUT(Binary));
  _4bit_OR _4bit_or_1 (.IF(Binary), .OUT(_4bit_or_1_out));
  _16bit_Calc_Subtract_Decode _16bit_calc_subtract_decode_1 (.I(Decode_Key), .out_2(Subtract));
  _16bit_Calc_Plus_Decode _16bit_calc_plus_decode_1 (.I(Decode_Key), .plus(Add));
  _16bit_Calc_CLR _16bit_calc_clr_1 (.I(Decode_Key), .CLR(CLEAR));
  _16bit_Calc_Equals _16bit_calc_equals_1 (.I(Decode_Key), .eq(Equals));
  or or_1 (or_1_out, _16_bit_5_bit_key_to_binary_1__0cycle, _4bit_or_1_out);
  and and_1 (and_1_out, Cycle_In, or_1_out);
  and and_2 (and_2_out, Subtract, Cycle_In);
  and and_3 (and_3_out, Add, Cycle_In);
  and and_4 (and_4_out, CLEAR, Cycle_In);
  and and_5 (and_5_out, Equals, Cycle_In);
  DiodeForward diodeforward_1 (.in(and_1_out), .out(Cycle_Out));
  DiodeForward diodeforward_2 (.in(and_2_out), .out(Cycle_Out));
  DiodeForward diodeforward_3 (.in(and_3_out), .out(Cycle_Out));
  DiodeForward diodeforward_4 (.in(and_4_out), .out(Cycle_Out));
  DiodeForward diodeforward_5 (.in(and_5_out), .out(Cycle_Out));
  PullDown pulldown_1 (.out(Cycle_Out));

  // Notes on the sheet:
  //   00001 - 1
  //   00010 - 2
  //   00011 - 3
  //   00100 - 4
  //   00101 - 5
  //   00110 - 6
  //   00111 - 7
  //   01000 - 8
  //   01001 - 9
  //   01010 - 0
  //   11000 - =
  //   10000 - +
  //   10100 - -
  //   11100 - CLR
endmodule
