// Digital circuit Mutllplier10Bit16.dig as structural Verilog
module Mutllplier10Bit16 (
  input  [15:0] K,
  output [15:0] O10x
);

  wire _16bitadder_1_of, pulldown_1_out;
  wire [15:0] offset1bit16_1_o1, offset3bit16_1_o3;

  Offset3Bit16 offset3bit16_1 (.F3(K), .O3(offset3bit16_1_o3));
  Offset1Bit16 offset1bit16_1 (.F1(K), .O1(offset1bit16_1_o1));
  _16BitAdder _16bitadder_1 (.A(offset3bit16_1_o3), .B(offset1bit16_1_o1), .Of(_16bitadder_1_of), .Sum(O10x));
  PullDown pulldown_1 (.out(pulldown_1_out));
  DiodeForward diodeforward_1 (.in(_16bitadder_1_of), .out(pulldown_1_out));

  // Notes on the sheet:
  //   K: Input for 10x multiplication
  //   O10x: Output for 10x Multiplication
endmodule
