// Digital circuit Offset1Bit16.dig as structural Verilog
module Offset1Bit16 (
  input  [15:0] F1,
  output [15:0] O1
);

  wire pulldown_1_out;

  PullDown pulldown_1 (.out(pulldown_1_out));
  DiodeForward diodeforward_1 (.in(F1[15]), .out(pulldown_1_out));

  assign O1 = {F1[14:0], 1'b0};

  // Notes on the sheet:
  //   F1: Offsets binary input by 1 bits to the right
endmodule
