// Digital circuit Offset3Bit16.dig as structural Verilog
module Offset3Bit16 (
  input  [15:0] F3,
  output [15:0] O3
);

  wire diodeforward_1_out, pulldown_1_out, pulldown_2_out;

  DiodeForward diodeforward_1 (.in(F3[13]), .out(diodeforward_1_out));
  PullDown pulldown_1 (.out(pulldown_1_out));
  DiodeForward diodeforward_2 (.in(F3[14]), .out(pulldown_1_out));
  PullDown pulldown_2 (.out(pulldown_2_out));
  DiodeForward diodeforward_3 (.in(F3[15]), .out(pulldown_2_out));
  PullDown pulldown_3 (.out(diodeforward_1_out));

  assign O3 = {F3[12:0], 3'b000};

  // Notes on the sheet:
  //   F3: Offsets binary input by 3 bits to the right
endmodule
