// Digital circuit SR-Latch-Q2-GND.dig as structural Verilog
module SR_Latch_Q2_GND (
  input  [15:0] Pressed_Input,
  input  Loop_IN,
  output Loop_Out
);

  wire or_1_out, or_2_out, or_3_out, rs_ff_as_1_nq;

  PullDown pulldown_1 (.out(Pressed_Input[15]));
  or or_1 (or_1_out, Pressed_Input[0], Pressed_Input[1]);
  or or_2 (or_2_out, or_1_out, Pressed_Input[2]);
  or or_3 (or_3_out, or_2_out, Pressed_Input[3]);
  RS_FF_AS rs_ff_as_1 (.S(or_3_out), .R(Loop_IN), .Q(Loop_Out), .nQ(rs_ff_as_1_nq));
  PullDown pulldown_2 (.out(rs_ff_as_1_nq));

  assign Pressed_Input[14:4] = {11{Pressed_Input[15]}};
endmodule
