// Digital circuit 16 bit calc redesign.dig as structural Verilog
module _16_bit_calc_redesign (
  output [15:0] out_1,
  output [15:0] out_2,
  output [15:0] out_3
);

  wire _0, _1, _2, _3, _4, _5, _6, _7, _8, _9, Add, ALU_Cycle, and_1_out, and_2_out, and_3_out, and_4_out,
       and_5_out, and_6_out, and_7_out, and_8_out, and_9_out, and_10_out, and_11_out, and_12_out, and_13_out,
       and_14_out, and_15_out, and_16_out, and_17_out, and_18_out, and_19_out, and_20_out, and_21_out,
       and_22_out, and_23_out, and_24_out, and_25_out, and_26_out, and_27_out, and_28_out, and_29_out,
       and_30_out, and_31_out, and_32_out, and_33_out, and_34_out, and_35_out, and_36_out, and_37_out,
       and_38_out, and_39_out, and_40_out, and_41_out, and_42_out, and_43_out, and_44_out, and_46_out,
       and_47_out, and_48_out, and_49_out, and_50_out, and_51_out, and_52_out, and_53_out, and_54_out,
       and_55_out, and_56_out, and_57_out, and_58_out, and_59_out, and_60_out, and_61_out, and_62_out,
       and_63_out, and_64_out, and_65_out, and_66_out, and_67_out, and_68_out, and_69_out, and_70_out,
       and_71_out, and_72_out, and_73_out, and_74_out, and_75_out, and_76_out, and_77_out, and_78_out,
       and_79_out, and_80_out, and_81_out, and_82_out, and_83_out, and_84_out, and_85_out, and_86_out,
       and_87_out, and_88_out, and_89_out, and_90_out, and_91_out, and_92_out, and_93_out, and_94_out,
       and_95_out, and_96_out, and_97_out, and_98_out, and_99_out, and_100_out, and_101_out, and_102_out,
       and_103_out, and_104_out, and_105_out, and_106_out, and_107_out, and_108_out, and_109_out,
       and_110_out, and_111_out, and_112_out, and_113_out, and_114_out, and_115_out, and_116_out,
       and_117_out, and_118_out, and_119_out, and_120_out, and_121_out, and_122_out, and_123_out,
       and_124_out, and_125_out, and_126_out, and_127_out, and_128_out, and_130_out, and_131_out,
       and_132_out, and_133_out, and_134_out, and_135_out, and_136_out, and_137_out, and_138_out,
       and_139_out, and_140_out, and_141_out, and_142_out, and_144_out, and_145_out, and_146_out,
       and_147_out, and_148_out, and_149_out, and_150_out, and_151_out, and_152_out, and_153_out,
       and_154_out, and_155_out, and_156_out, and_157_out, and_158_out, and_159_out, and_160_out,
       and_161_out, and_162_out, and_163_out, and_164_out, and_165_out, and_166_out, and_167_out,
       and_168_out, and_169_out, and_170_out, and_171_out, and_172_out, and_173_out, and_174_out,
       and_175_out, and_176_out, and_177_out, and_178_out, and_179_out, and_180_out, and_181_out,
       and_182_out, and_183_out, bcd_gate_2_o_1, bcd_gate_2_o_2, bcd_gate_2_o_3, bcd_gate_2_o_4,
       bcd_gate_3_o_1, bcd_gate_3_o_2, bcd_gate_3_o_3, bcd_gate_3_o_4, bcd_gate_5_o_1, bcd_gate_5_o_2,
       bcd_gate_5_o_3, bcd_gate_5_o_4, bcd_gate_6_o_1, bcd_gate_6_o_2, bcd_gate_6_o_3, bcd_gate_6_o_4,
       bcd_gate_7_o_1, bcd_gate_7_o_2, bcd_gate_7_o_3, bcd_gate_7_o_4, bcd_gate_8_o_1, bcd_gate_8_o_2,
       bcd_gate_8_o_3, bcd_gate_8_o_4, bcd_gate_9_o_1, bcd_gate_9_o_2, bcd_gate_9_o_3, bcd_gate_9_o_4,
       bcd_gate_10_o_1, bcd_gate_10_o_2, bcd_gate_10_o_3, bcd_gate_10_o_4, bcd_gate_12_o_1, bcd_gate_12_o_2,
       bcd_gate_12_o_3, bcd_gate_12_o_4, bcd_gate_13_o_1, bcd_gate_13_o_2, bcd_gate_13_o_3, bcd_gate_13_o_4,
       bcd_gate_14_o_1, bcd_gate_14_o_2, bcd_gate_14_o_3, bcd_gate_14_o_4, bcd_gate_15_o_1, bcd_gate_15_o_2,
       bcd_gate_15_o_3, bcd_gate_15_o_4, bcd_gate_16_o_1, bcd_gate_16_o_2, bcd_gate_16_o_3, bcd_gate_16_o_4,
       bcd_gate_17_o_1, bcd_gate_17_o_2, bcd_gate_17_o_3, bcd_gate_17_o_4, bcd_gate_18_o_1, bcd_gate_18_o_2,
       bcd_gate_18_o_3, bcd_gate_18_o_4, bcd_gate_19_o_1, bcd_gate_19_o_2, bcd_gate_19_o_3, bcd_gate_19_o_4,
       bcd_gate_20_o_1, bcd_gate_20_o_2, bcd_gate_20_o_3, bcd_gate_20_o_4, bcd_gate_21_o_1, bcd_gate_21_o_2,
       bcd_gate_21_o_3, bcd_gate_21_o_4, bcd_gate_23_o_1, bcd_gate_23_o_2, bcd_gate_23_o_3, bcd_gate_23_o_4,
       bcd_gate_24_o_1, bcd_gate_24_o_2, bcd_gate_24_o_3, bcd_gate_24_o_4, bcd_gate_25_o_1, bcd_gate_25_o_2,
       bcd_gate_25_o_3, bcd_gate_25_o_4, bcd_gate_26_o_1, bcd_gate_26_o_2, bcd_gate_26_o_3, bcd_gate_26_o_4,
       bcd_gate_27_o_1, bcd_gate_27_o_2, bcd_gate_27_o_3, bcd_gate_27_o_4, bcd_gate_28_o_1, bcd_gate_28_o_2,
       bcd_gate_28_o_3, bcd_gate_28_o_4, bcd_gate_29_o_1, bcd_gate_29_o_2, bcd_gate_29_o_3, bcd_gate_29_o_4,
       bcd_gate_30_o_1, bcd_gate_30_o_2, bcd_gate_30_o_3, bcd_gate_30_o_4, bcd_gate_31_o_1, bcd_gate_31_o_2,
       bcd_gate_31_o_3, bcd_gate_31_o_4, bcd_gate_32_o_1, bcd_gate_32_o_2, bcd_gate_32_o_3, bcd_gate_32_o_4,
       bcd_gate_33_o_1, bcd_gate_33_o_2, bcd_gate_33_o_3, bcd_gate_33_o_4, bcd_gate_34_o_1, bcd_gate_34_o_2,
       bcd_gate_34_o_3, bcd_gate_34_o_4, bcd_gate_35_o_1, bcd_gate_35_o_2, bcd_gate_35_o_3, bcd_gate_35_o_4,
       bcd_gate_37_o_1, bcd_gate_37_o_2, bcd_gate_37_o_3, bcd_gate_37_o_4, bcd_gate_38_o_1, bcd_gate_38_o_2,
       bcd_gate_38_o_3, bcd_gate_38_o_4, bcd_gate_39_o_1, bcd_gate_39_o_2, bcd_gate_39_o_3, bcd_gate_39_o_4,
       bcd_gate_40_o_1, bcd_gate_40_o_2, bcd_gate_40_o_3, bcd_gate_40_o_4, Carry1, Carry2, Carry3, Carry4,
       Carry5, Carry6, Carry7, Carry8, Carry9, Carry10, Carry11, Carry12, Carry13, Carry14, Carry15, Clear,
       CLR, Cycle_1, Cycle_2, cycle_2_5, Cycle_3, delay_1_out, delay_2_out, delay_3_out, delay_5_out,
       delay_7_out, delay_8_out, delay_9_out, delay_10_out, delay_11_out, delay_13_out, delay_15_out,
       delay_16_out, delay_17_out, delay_18_out, delay_19_out, delay_20_out, delay_21_out, delay_22_out,
       delay_23_out, delay_24_out, delay_25_out, delay_26_out, delay_27_out, delay_28_out, delay_29_out,
       delay_30_out, delay_31_out, delay_32_out, delay_33_out, delay_35_out, delay_36_out, delay_37_out,
       diodeforward_11_out, diodeforward_12_out, diodeforward_14_out, diodeforward_43_out,
       diodeforward_46_out, diodeforward_53_out, diodeforward_54_out, diodeforward_55_out,
       diodeforward_58_out, DS_I_1, DS_I_2, DS_I_3, DS_I_4, DS_I_5, DS_I_6, DS_I_8, DS_I_9, DS_I_10, DS_I_11,
       DS_I_12, DS_I_13, DS_I_15, DS_I_16, DS_I_17, DS_I_18, DS_I_19, DS_I_20, DS_I_22, DS_I_23, DS_I_24,
       DS_I_25, DS_I_26, DS_I_27, DS_I_29, DS_I_30, DS_I_31, DS_I_32, DS_I_33, DS_I_34, DS_I_36, DS_I_37,
       DS_I_38, DS_I_39, DS_I_40, eq, Equal, InputA1, InputA2, InputA3, InputA4, InputA5, InputA6, InputA7,
       InputA8, InputA9, InputA10, InputA11, InputA12, InputA13, InputA14, InputA15, InputA16, InputB1,
       InputB2, InputB3, InputB4, InputB5, InputB6, InputB7, InputB8, InputB9, InputB10, InputB11, InputB12,
       InputB13, InputB14, InputB15, InputB16, Keypad_press, multiplexer_5_out, multiplexer_6_out, Negative,
       not_1_out, not_2_out, not_3_out, not_4_out, not_5_out, not_6_out, not_7_out, not_8_out, not_9_out,
       not_10_out, not_11_out, not_12_out, not_13_out, not_14_out, not_15_out, not_16_out, not_17_out,
       not_18_out, not_19_out, not_20_out, not_21_out, not_22_out, not_23_out, not_24_out, not_25_out,
       not_26_out, not_27_out, not_28_out, not_29_out, not_30_out, not_32_out, not_33_out, not_34_out,
       not_35_out, not_36_out, not_37_out, Operator_Pressed, or_15_out, or_17_out, or_24_out, or_25_out,
       or_26_out, or_27_out, or_28_out, or_30_out, or_31_out, or_32_out, or_39_out, or_40_out, or_41_out,
       or_42_out, or_43_out, or_44_out, or_45_out, or_48_out, or_49_out, or_50_out, or_51_out, or_57_out,
       or_58_out, or_59_out, or_60_out, or_61_out, or_62_out, or_63_out, or_64_out, or_65_out, or_74_out,
       or_75_out, or_85_out, plus, pulldown_1_out, pulldown_3_out, pulldown_12_out, pulldown_19_out,
       pulldown_20_out, pulldown_21_out, pulldown_22_out, pulldown_24_out, pulldown_25_out, pulldown_26_out,
       pulldown_27_out, pulldown_28_out, rs_ff_as_1_nq, rs_ff_as_1_q, rs_ff_as_2_nq, rs_ff_as_3_q,
       rs_ff_as_4_q, Shift_Cycle, Sub, Sub_process, tunnel, xor_1_out, xor_2_out, xor_3_out, xor_5_out,
       xor_6_out, xor_7_out, xor_8_out, xor_9_out, xor_10_out, xor_11_out, xor_12_out, xor_13_out,
       xor_14_out, xor_23_out, xor_25_out, xor_26_out, xor_27_out, xor_28_out, xor_29_out, xor_30_out,
       xor_31_out, xor_32_out, xor_33_out, xor_34_out, Zero_C;
  wire [2:0] ALU_MUX;
  wire [3:0] Binary_1, Hundreds, Hundreds__of_Thousands, Ones, Tens, Tens_of_Thousands, Thousands;
  wire [4:0] Cycle_Register_q, diodeforward_15_out, multiplexer_2_out;
  wire [7:0] Output_9_16, xor_19_out;
  wire [14:0] multiplexer_3_out;
  wire [15:0] _10x_BIN, ALU_B, multiplexer_10_out, multiplexer_11_out, multiplexer_13_out,
       multiplexer_14_out, not_31_out, not_38_out, pulldown_31_out, pulldown_34_out, pulldown_35_out,
       pulldown_36_out, pulldown_39_out, Reg_A_In, S, subtracted, Sum_3, sum_4, T1, Temp_in;
  wire [15:1] multiplexer_4_out;

  not not_1 (not_1_out, Tens_of_Thousands[3]);
  not not_2 (not_2_out, Tens_of_Thousands[2]);
  not not_3 (not_3_out, Tens_of_Thousands[1]);
  PullDown pulldown_1 (.out(pulldown_1_out));
  not not_4 (not_4_out, Tens_of_Thousands[0]);
  and and_1 (and_1_out, Tens_of_Thousands[3], Tens_of_Thousands[0]);
  and and_2 (and_2_out, not_1_out, Tens_of_Thousands[1]);
  and and_3 (and_3_out, Tens_of_Thousands[2], Tens_of_Thousands[0]);
  and and_4 (and_4_out, not_2_out, not_3_out, not_4_out);
  and and_5 (and_5_out, not_1_out, not_2_out);
  and and_6 (and_6_out, not_2_out, Tens_of_Thousands[0]);
  and and_7 (and_7_out, not_3_out, not_4_out);
  and and_8 (and_8_out, Tens_of_Thousands[1], Tens_of_Thousands[0]);
  or or_1 (DS_I_40, Tens_of_Thousands[2], not_3_out, Tens_of_Thousands[0]);
  and and_9 (and_9_out, not_1_out, Tens_of_Thousands[1], not_4_out);
  and and_10 (and_10_out, Tens_of_Thousands[2], not_3_out, Tens_of_Thousands[0]);
  and and_11 (and_11_out, not_2_out, not_3_out, not_4_out);
  and and_12 (and_12_out, not_2_out, Tens_of_Thousands[1], Tens_of_Thousands[0]);
  and and_13 (and_13_out, not_1_out, Tens_of_Thousands[1], not_4_out);
  and and_14 (and_14_out, not_2_out, not_3_out, not_4_out);
  and and_15 (and_15_out, Tens_of_Thousands[3], Tens_of_Thousands[0]);
  and and_16 (and_16_out, Tens_of_Thousands[2], not_3_out);
  and and_17 (and_17_out, Tens_of_Thousands[2], not_4_out);
  and and_18 (and_18_out, not_3_out, not_4_out);
  and and_19 (and_19_out, Tens_of_Thousands[3], not_3_out);
  and and_20 (and_20_out, not_1_out, not_2_out, Tens_of_Thousands[1]);
  and and_21 (and_21_out, Tens_of_Thousands[2], not_3_out);
  and and_22 (and_22_out, Tens_of_Thousands[2], not_4_out);
  Seven_Seg seven_seg_1 (
    .a(pulldown_1_out), .b(pulldown_1_out), .c(pulldown_1_out), .d(pulldown_1_out), .e(pulldown_1_out),
    .f(pulldown_1_out), .g(Negative), .dp(pulldown_1_out));
  Seven_Seg seven_seg_2 (
    .a(DS_I_29), .b(DS_I_30), .c(DS_I_40), .d(DS_I_31), .e(DS_I_32), .f(DS_I_33), .g(DS_I_34), .dp(1'b0));
  Button u__7 (.out(_7));
  DiodeForward diodeforward_1 (.in(_7), .out(Keypad_press));
  Button u__4 (.out(_4));
  DiodeForward diodeforward_2 (.in(_4), .out(Keypad_press));
  Button u__1 (.out(_1));
  DiodeForward diodeforward_3 (.in(_1), .out(Keypad_press));
  or or_2 (DS_I_29, and_1_out, and_2_out, and_3_out, and_4_out);
  or or_3 (DS_I_30, and_5_out, and_6_out, and_7_out, and_8_out);
  or or_4 (DS_I_31, and_9_out, and_10_out, and_11_out, and_12_out);
  or or_5 (DS_I_32, and_13_out, and_14_out);
  or or_6 (DS_I_33, and_15_out, and_16_out, and_17_out, and_18_out);
  or or_7 (DS_I_34, and_19_out, and_20_out, and_21_out, and_22_out);
  Seven_Seg seven_seg_3 (
    .a(DS_I_22), .b(DS_I_23), .c(DS_I_39), .d(DS_I_24), .e(DS_I_25), .f(DS_I_26), .g(DS_I_27), .dp(1'b0));
  Button u__8 (.out(_8));
  Button u__5 (.out(_5));
  Button u__2 (.out(_2));
  Button u__0 (.out(_0));
  DiodeForward diodeforward_4 (.in(_8), .out(Keypad_press));
  DiodeForward diodeforward_5 (.in(_5), .out(Keypad_press));
  DiodeForward diodeforward_6 (.in(_2), .out(Keypad_press));
  DiodeForward diodeforward_7 (.in(_0), .out(Keypad_press));
  not not_5 (not_5_out, Thousands[3]);
  Seven_Seg seven_seg_4 (
    .a(DS_I_15), .b(DS_I_16), .c(DS_I_38), .d(DS_I_17), .e(DS_I_18), .f(DS_I_19), .g(DS_I_20), .dp(1'b0));
  Button u__9 (.out(_9));
  DiodeForward diodeforward_8 (.in(_9), .out(Keypad_press));
  Button u__6 (.out(_6));
  DiodeForward diodeforward_9 (.in(_6), .out(Keypad_press));
  Button u__3 (.out(_3));
  DiodeForward diodeforward_10 (.in(_3), .out(Keypad_press));
  not not_6 (not_6_out, Thousands[2]);
  Seven_Seg seven_seg_5 (
    .a(DS_I_8), .b(DS_I_9), .c(DS_I_37), .d(DS_I_10), .e(DS_I_11), .f(DS_I_12), .g(DS_I_13), .dp(1'b0));
  not not_7 (not_7_out, Thousands[1]);
  Seven_Seg seven_seg_6 (
    .a(DS_I_1), .b(DS_I_2), .c(DS_I_36), .d(DS_I_3), .e(DS_I_4), .f(DS_I_5), .g(DS_I_6), .dp(1'b0));
  Button u_plus (.out(plus));
  Button button (.out(tunnel));
  Button u_eq (.out(eq));
  Button u_CLR (.out(CLR));
  not not_8 (not_8_out, Thousands[0]);
  and and_23 (and_23_out, Thousands[3], Thousands[0]);
  and and_24 (and_24_out, not_5_out, Thousands[1]);
  and and_25 (and_25_out, Thousands[2], Thousands[0]);
  and and_26 (and_26_out, not_6_out, not_7_out, not_8_out);
  and and_27 (and_27_out, not_5_out, not_6_out);
  and and_28 (and_28_out, not_6_out, Thousands[0]);
  and and_29 (and_29_out, not_7_out, not_8_out);
  and and_30 (and_30_out, Thousands[1], Thousands[0]);
  or or_8 (DS_I_39, Thousands[2], not_7_out, Thousands[0]);
  and and_31 (and_31_out, not_5_out, Thousands[1], not_8_out);
  and and_32 (and_32_out, Thousands[2], not_7_out, Thousands[0]);
  and and_33 (and_33_out, not_6_out, not_7_out, not_8_out);
  and and_34 (and_34_out, not_6_out, Thousands[1], Thousands[0]);
  and and_35 (and_35_out, not_5_out, Thousands[1], not_8_out);
  and and_36 (and_36_out, not_6_out, not_7_out, not_8_out);
  and and_37 (and_37_out, Thousands[3], Thousands[0]);
  and and_38 (and_38_out, Thousands[2], not_7_out);
  and and_39 (and_39_out, Thousands[2], not_8_out);
  and and_40 (and_40_out, not_7_out, not_8_out);
  and and_41 (and_41_out, Thousands[3], not_7_out);
  and and_42 (and_42_out, not_5_out, not_6_out, Thousands[1]);
  and and_43 (and_43_out, Thousands[2], not_7_out);
  and and_44 (and_44_out, Thousands[2], not_8_out);
  PullDown pulldown_2 (.out(Keypad_press));
  or or_9 (DS_I_22, and_23_out, and_24_out, and_25_out, and_26_out);
  or or_10 (DS_I_23, and_27_out, and_28_out, and_29_out, and_30_out);
  or or_11 (DS_I_24, and_31_out, and_32_out, and_33_out, and_34_out);
  or or_12 (DS_I_25, and_35_out, and_36_out);
  or or_13 (DS_I_26, and_37_out, and_38_out, and_39_out, and_40_out);
  or or_14 (DS_I_27, and_41_out, and_42_out, and_43_out, and_44_out);
  not not_9 (not_9_out, Hundreds[3]);
  not not_10 (not_10_out, Hundreds[2]);
  not not_11 (not_11_out, Hundreds[1]);
  and and_45 (Zero_C, not_12_out, and_68_out);
  not not_12 (not_12_out, or_15_out);
  or or_15 (or_15_out, diodeforward_15_out[2], diodeforward_15_out[4], diodeforward_15_out[0]);
  not not_13 (not_13_out, Hundreds[0]);
  and and_46 (and_46_out, Hundreds[3], Hundreds[0]);
  and and_47 (and_47_out, not_9_out, Hundreds[1]);
  and and_48 (and_48_out, Hundreds[2], Hundreds[0]);
  and and_49 (and_49_out, not_10_out, not_11_out, not_13_out);
  and and_50 (and_50_out, not_9_out, not_10_out);
  and and_51 (and_51_out, not_10_out, Hundreds[0]);
  and and_52 (and_52_out, not_11_out, not_13_out);
  and and_53 (and_53_out, Hundreds[1], Hundreds[0]);
  or or_16 (DS_I_38, Hundreds[2], not_11_out, Hundreds[0]);
  and and_54 (and_54_out, not_9_out, Hundreds[1], not_13_out);
  and and_55 (and_55_out, Hundreds[2], not_11_out, Hundreds[0]);
  and and_56 (and_56_out, not_10_out, not_11_out, not_13_out);
  and and_57 (and_57_out, not_10_out, Hundreds[1], Hundreds[0]);
  and and_58 (and_58_out, not_9_out, Hundreds[1], not_13_out);
  and and_59 (and_59_out, not_10_out, not_11_out, not_13_out);
  and and_60 (and_60_out, Hundreds[3], Hundreds[0]);
  and and_61 (and_61_out, Hundreds[2], not_11_out);
  and and_62 (and_62_out, Hundreds[2], not_13_out);
  and and_63 (and_63_out, not_11_out, not_13_out);
  and and_64 (and_64_out, Hundreds[3], not_11_out);
  and and_65 (and_65_out, not_9_out, not_10_out, Hundreds[1]);
  and and_66 (and_66_out, Hundreds[2], not_11_out);
  and and_67 (and_67_out, Hundreds[2], not_13_out);
  DiodeForward diodeforward_11 (.in(out_1[13]), .out(diodeforward_11_out));
  DiodeForward diodeforward_12 (.in(out_1[14]), .out(diodeforward_12_out));
  PullDown pulldown_3 (.out(pulldown_3_out));
  DiodeForward diodeforward_13 (.in(out_1[15]), .out(pulldown_3_out));
  DiodeForward diodeforward_14 (.in(out_1[15]), .out(diodeforward_14_out));
  Delay #(.delayTime(20)) delay_1 (.in(Cycle_2), .out(delay_1_out));
  and and_68 (and_68_out, diodeforward_15_out[1], diodeforward_15_out[3]);
  PullDown pulldown_4 (.out(diodeforward_11_out));
  PullDown pulldown_5 (.out(diodeforward_12_out));
  PullDown pulldown_6 (.out(diodeforward_14_out));
  Register #(.Bits(16)) register_1 (.D(Sum_3), .C(delay_1_out), .en(Cycle_1), .Q(_10x_BIN));
  DiodeForward diodeforward_15 (.in(_0), .out(diodeforward_15_out[3]));
  or or_17 (or_17_out, diodeforward_15_out[0], diodeforward_15_out[1]);
  or or_18 (DS_I_15, and_46_out, and_47_out, and_48_out, and_49_out);
  or or_19 (DS_I_16, and_50_out, and_51_out, and_52_out, and_53_out);
  or or_20 (DS_I_17, and_54_out, and_55_out, and_56_out, and_57_out);
  or or_21 (DS_I_18, and_58_out, and_59_out);
  or or_22 (DS_I_19, and_60_out, and_61_out, and_62_out, and_63_out);
  or or_23 (DS_I_20, and_64_out, and_65_out, and_66_out, and_67_out);
  DiodeForward diodeforward_16 (.in(_0), .out(diodeforward_15_out[1]));
  DiodeForward diodeforward_17 (.in(_9), .out(diodeforward_15_out[3]));
  DiodeForward diodeforward_18 (.in(_9), .out(diodeforward_15_out[0]));
  or or_24 (or_24_out, or_17_out, diodeforward_15_out[2]);
  DiodeForward diodeforward_19 (.in(CLR), .out(diodeforward_15_out[3]));
  DiodeForward diodeforward_20 (.in(CLR), .out(diodeforward_15_out[2]));
  DiodeForward diodeforward_21 (.in(_8), .out(diodeforward_15_out[3]));
  DiodeForward diodeforward_22 (.in(_7), .out(diodeforward_15_out[1]));
  DiodeForward diodeforward_23 (.in(_7), .out(diodeforward_15_out[2]));
  DiodeForward diodeforward_24 (.in(_7), .out(diodeforward_15_out[0]));
  DiodeForward diodeforward_25 (.in(CLR), .out(diodeforward_15_out[4]));
  DiodeForward diodeforward_26 (.in(_5), .out(diodeforward_15_out[2]));
  DiodeForward diodeforward_27 (.in(_6), .out(diodeforward_15_out[2]));
  DiodeForward diodeforward_28 (.in(_6), .out(diodeforward_15_out[1]));
  or or_25 (or_25_out, or_24_out, diodeforward_15_out[3]);
  not not_14 (not_14_out, Tens[3]);
  not not_15 (not_15_out, Tens[2]);
  or or_26 (or_26_out, Binary_1[0], Binary_1[1]);
  DiodeForward diodeforward_29 (.in(tunnel), .out(diodeforward_15_out[4]));
  DiodeForward diodeforward_30 (.in(tunnel), .out(diodeforward_15_out[2]));
  DiodeForward diodeforward_31 (.in(_4), .out(diodeforward_15_out[2]));
  DiodeForward diodeforward_32 (.in(_5), .out(diodeforward_15_out[0]));
  or or_27 (or_27_out, or_25_out, diodeforward_15_out[4]);
  not not_16 (not_16_out, Tens[1]);
  or or_28 (or_28_out, or_26_out, Binary_1[2]);
  DiodeForward diodeforward_33 (.in(plus), .out(diodeforward_15_out[4]));
  DiodeForward diodeforward_34 (.in(_2), .out(diodeforward_15_out[1]));
  DiodeForward diodeforward_35 (.in(_3), .out(diodeforward_15_out[1]));
  DiodeForward diodeforward_36 (.in(_3), .out(diodeforward_15_out[0]));
  not not_17 (not_17_out, or_27_out);
  not not_18 (not_18_out, Tens[0]);
  and and_69 (and_69_out, Tens[3], Tens[0]);
  and and_70 (and_70_out, not_14_out, Tens[1]);
  and and_71 (and_71_out, Tens[2], Tens[0]);
  and and_72 (and_72_out, not_15_out, not_16_out, not_18_out);
  and and_73 (and_73_out, not_14_out, not_15_out);
  and and_74 (and_74_out, not_15_out, Tens[0]);
  and and_75 (and_75_out, not_16_out, not_18_out);
  and and_76 (and_76_out, Tens[1], Tens[0]);
  or or_29 (DS_I_37, Tens[2], not_16_out, Tens[0]);
  and and_77 (and_77_out, not_14_out, Tens[1], not_18_out);
  and and_78 (and_78_out, Tens[2], not_16_out, Tens[0]);
  and and_79 (and_79_out, not_15_out, not_16_out, not_18_out);
  and and_80 (and_80_out, not_15_out, Tens[1], Tens[0]);
  and and_81 (and_81_out, not_14_out, Tens[1], not_18_out);
  and and_82 (and_82_out, not_15_out, not_16_out, not_18_out);
  and and_83 (and_83_out, Tens[3], Tens[0]);
  and and_84 (and_84_out, Tens[2], not_16_out);
  and and_85 (and_85_out, Tens[2], not_18_out);
  and and_86 (and_86_out, not_16_out, not_18_out);
  and and_87 (and_87_out, Tens[3], not_16_out);
  and and_88 (and_88_out, not_14_out, not_15_out, Tens[1]);
  and and_89 (and_89_out, Tens[2], not_16_out);
  and and_90 (and_90_out, Tens[2], not_18_out);
  or or_30 (or_30_out, or_28_out, Binary_1[3]);
  DiodeForward diodeforward_37 (.in(eq), .out(diodeforward_15_out[3]));
  DiodeForward diodeforward_38 (.in(eq), .out(diodeforward_15_out[4]));
  PullDown pulldown_7 (.out(diodeforward_15_out[4]));
  PullDown pulldown_8 (.out(diodeforward_15_out[3]));
  PullDown pulldown_9 (.out(diodeforward_15_out[2]));
  PullDown pulldown_10 (.out(diodeforward_15_out[1]));
  PullDown pulldown_11 (.out(diodeforward_15_out[0]));
  DiodeForward diodeforward_39 (.in(_1), .out(diodeforward_15_out[0]));
  and and_91 (and_91_out, not_17_out, Cycle_1);
  xor xor_1 (xor_1_out, Cycle_1, or_27_out);
  and and_92 (and_92_out, not_19_out, and_94_out);
  not not_19 (not_19_out, or_31_out);
  or or_31 (or_31_out, or_32_out, multiplexer_2_out[2]);
  or or_32 (or_32_out, multiplexer_2_out[0], multiplexer_2_out[1]);
  PullDown pulldown_12 (.out(pulldown_12_out));
  not not_20 (not_20_out, 1'b0);
  and and_93 (and_93_out, Cycle_3, not_17_out);
  xor xor_2 (xor_2_out, and_91_out, xor_1_out);
  or or_33 (DS_I_8, and_69_out, and_70_out, and_71_out, and_72_out);
  or or_34 (DS_I_9, and_73_out, and_74_out, and_75_out, and_76_out);
  or or_35 (DS_I_10, and_77_out, and_78_out, and_79_out, and_80_out);
  or or_36 (DS_I_11, and_81_out, and_82_out);
  or or_37 (DS_I_12, and_83_out, and_84_out, and_85_out, and_86_out);
  or or_38 (DS_I_13, and_87_out, and_88_out, and_89_out, and_90_out);
  and and_94 (and_94_out, multiplexer_2_out[3], multiplexer_2_out[4]);
  DiodeForward diodeforward_40 (.in(or_30_out), .out(pulldown_12_out));
  DiodeForward diodeforward_41 (.in(delay_3_out), .out(pulldown_12_out));
  and and_95 (and_95_out, pulldown_12_out, not_20_out);
  or or_39 (or_39_out, or_40_out, multiplexer_2_out[3]);
  or or_40 (or_40_out, or_41_out, multiplexer_2_out[2]);
  or or_41 (or_41_out, multiplexer_2_out[0], multiplexer_2_out[1]);
  Delay #(.delayTime(20)) delay_2 (.in(Zero_C), .out(delay_2_out));
  Delay #(.delayTime(20)) delay_3 (.in(delay_2_out), .out(delay_3_out));
  RS_FF_AS rs_ff_as_1 (.S(xor_2_out), .R(Cycle_1), .Q(rs_ff_as_1_q), .nQ(rs_ff_as_1_nq));
  DiodeForward diodeforward_42 (.in(rs_ff_as_1_q), .out(Cycle_1));
  or or_42 (or_42_out, and_92_out, and_96_out, and_98_out);
  and and_96 (and_96_out, not_21_out, multiplexer_2_out[4]);
  not not_21 (not_21_out, or_39_out);
  Multiplexer #(.Bits(16)) multiplexer_1 (.sel(and_97_out), .in_0({16{1'b0}}), .in_1(sum_4), .out(Reg_A_In));
  DiodeForward diodeforward_43 (.in(rs_ff_as_1_q), .out(diodeforward_43_out));
  DiodeForward diodeforward_44 (.in(Cycle_1), .out(diodeforward_43_out));
  PullDown pulldown_13 (.out(Cycle_1));
  not not_22 (not_22_out, Ones[3]);
  or or_43 (or_43_out, or_44_out, multiplexer_2_out[3]);
  or or_44 (or_44_out, multiplexer_2_out[0], multiplexer_2_out[1]);
  Delay #(.delayTime(20)) delay_4 (.in(Cycle_2), .out(cycle_2_5));
  Delay #(.delayTime(20)) delay_5 (.in(cycle_2_5), .out(delay_5_out));
  and and_97 (and_97_out, delay_5_out, and_95_out);
  Delay #(.delayTime(6)) delay_6 (.in(and_97_out), .out(Shift_Cycle));
  RS_FF_AS rs_ff_as_2 (.S(rs_ff_as_1_q), .R(and_93_out), .Q(Cycle_1), .nQ(rs_ff_as_2_nq));
  PullDown pulldown_14 (.out(rs_ff_as_1_nq));
  PullDown pulldown_15 (.out(diodeforward_43_out));
  PullDown pulldown_16 (.out(diodeforward_43_out));
  not not_23 (not_23_out, Ones[2]);
  and and_98 (and_98_out, not_24_out, and_99_out);
  not not_24 (not_24_out, or_43_out);
  PullDown pulldown_17 (.out(Shift_Cycle));
  PullDown pulldown_18 (.out(rs_ff_as_2_nq));
  DiodeForward diodeforward_45 (.in(and_93_out), .out(diodeforward_43_out));
  Register #(.Bits(5)) Cycle_Register (
    .D(diodeforward_15_out), .C(diodeforward_43_out), .en(diodeforward_43_out), .Q(Cycle_Register_q));
  not not_25 (not_25_out, Ones[1]);
  not not_26 (not_26_out, Ones[0]);
  or or_45 (or_45_out, multiplexer_2_out[4], or_42_out);
  and and_99 (and_99_out, multiplexer_2_out[2], multiplexer_2_out[4]);
  and and_100 (and_100_out, Ones[3], Ones[0]);
  and and_101 (and_101_out, not_22_out, Ones[1]);
  and and_102 (and_102_out, Ones[2], Ones[0]);
  and and_103 (and_103_out, not_23_out, not_25_out, not_26_out);
  and and_104 (and_104_out, not_22_out, not_23_out);
  and and_105 (and_105_out, not_23_out, Ones[0]);
  and and_106 (and_106_out, not_25_out, not_26_out);
  and and_107 (and_107_out, Ones[1], Ones[0]);
  or or_46 (DS_I_36, Ones[2], not_25_out, Ones[0]);
  and and_108 (and_108_out, not_22_out, Ones[1], not_26_out);
  and and_109 (and_109_out, Ones[2], not_25_out, Ones[0]);
  and and_110 (and_110_out, not_23_out, not_25_out, not_26_out);
  and and_111 (and_111_out, not_23_out, Ones[1], Ones[0]);
  and and_112 (and_112_out, not_22_out, Ones[1], not_26_out);
  and and_113 (and_113_out, not_23_out, not_25_out, not_26_out);
  and and_114 (and_114_out, Ones[3], Ones[0]);
  and and_115 (and_115_out, Ones[2], not_25_out);
  and and_116 (and_116_out, Ones[2], not_26_out);
  and and_117 (and_117_out, not_25_out, not_26_out);
  and and_118 (and_118_out, Ones[3], not_25_out);
  and and_119 (and_119_out, not_22_out, not_23_out, Ones[1]);
  and and_120 (and_120_out, Ones[2], not_25_out);
  and and_121 (and_121_out, Ones[2], not_26_out);
  not not_27 (not_27_out, or_45_out);
  Multiplexer #(.Bits(5)) multiplexer_2 (
    .sel(not_28_out), .in_0(Cycle_Register_q), .in_1({5{1'b0}}), .out(multiplexer_2_out));
  not not_28 (not_28_out, Cycle_1);
  or or_47 (DS_I_4, and_112_out, and_113_out);
  RS_FF_AS rs_ff_as_3 (.S(Operator_Pressed), .R(Keypad_press), .Q(rs_ff_as_3_q));  // open: nQ
  and and_122 (and_122_out, multiplexer_2_out[3], not_27_out);
  or or_48 (or_48_out, multiplexer_2_out[0], multiplexer_2_out[1]);
  or or_49 (or_49_out, multiplexer_2_out[0], multiplexer_2_out[1]);
  or or_50 (or_50_out, multiplexer_2_out[0], multiplexer_2_out[1]);
  or or_51 (or_51_out, multiplexer_2_out[0], multiplexer_2_out[1]);
  or or_52 (DS_I_1, and_100_out, and_101_out, and_102_out, and_103_out);
  or or_53 (DS_I_2, and_104_out, and_105_out, and_106_out, and_107_out);
  or or_54 (DS_I_3, and_108_out, and_109_out, and_110_out, and_111_out);
  or or_55 (DS_I_5, and_114_out, and_115_out, and_116_out, and_117_out);
  or or_56 (DS_I_6, and_118_out, and_119_out, and_120_out, and_121_out);
  and and_123 (and_123_out, multiplexer_2_out[2], not_27_out);
  or or_57 (or_57_out, or_48_out, multiplexer_2_out[3]);
  or or_58 (or_58_out, or_49_out, multiplexer_2_out[2]);
  not not_29 (not_29_out, or_50_out);
  and and_124 (and_124_out, multiplexer_2_out[2], multiplexer_2_out[3], multiplexer_2_out[4]);
  or or_59 (or_59_out, or_51_out, multiplexer_2_out[2]);
  and and_125 (and_125_out, multiplexer_2_out[3], multiplexer_2_out[4]);
  Multiplexer #(.Bits(16)) multiplexer_3 (
    .sel(rs_ff_as_3_q), .in_0(out_1), .in_1(out_2), .out({Negative, multiplexer_3_out}));
  and and_126 (and_126_out, multiplexer_2_out[1], not_27_out);
  or or_60 (or_60_out, or_58_out, multiplexer_2_out[3]);
  Delay #(.delayTime(3)) delay_7 (.in(and_125_out), .out(delay_7_out));
  Multiplexer #(.Bits(16)) multiplexer_4 (
    .sel(Negative), .in_0({Negative, multiplexer_3_out}), .in_1(not_31_out),
    .out({multiplexer_4_out, Ones[0]}));
  and and_127 (and_127_out, multiplexer_2_out[0], not_27_out);
  not not_30 (not_30_out, or_57_out);
  and and_128 (and_128_out, multiplexer_2_out[2], multiplexer_2_out[4]);
  Delay #(.delayTime(5)) delay_8 (.in(multiplexer_2_out[4]), .out(delay_8_out));
  Delay #(.delayTime(2)) delay_9 (.in(and_124_out), .out(delay_9_out));
  BCD_Gate bcd_gate_1 (
    .B_1(multiplexer_4_out[1]), .B_2(bcd_gate_2_o_1), .B_3(bcd_gate_2_o_2), .B_4(bcd_gate_2_o_3),
    .O_1(Ones[1]), .O_2(Ones[2]), .O_3(Ones[3]), .O_4(Tens[0]));
  BCD_Gate bcd_gate_2 (
    .B_1(multiplexer_4_out[2]), .B_2(bcd_gate_3_o_1), .B_3(bcd_gate_3_o_2), .B_4(bcd_gate_3_o_3),
    .O_1(bcd_gate_2_o_1), .O_2(bcd_gate_2_o_2), .O_3(bcd_gate_2_o_3), .O_4(bcd_gate_2_o_4));
  BCD_Gate bcd_gate_3 (
    .B_1(multiplexer_4_out[3]), .B_2(bcd_gate_7_o_1), .B_3(bcd_gate_7_o_2), .B_4(bcd_gate_7_o_3),
    .O_1(bcd_gate_3_o_1), .O_2(bcd_gate_3_o_2), .O_3(bcd_gate_3_o_3), .O_4(bcd_gate_3_o_4));
  assign not_31_out = ~{Negative, multiplexer_3_out};  // Not not_31, 16 bits wide
  not not_32 (not_32_out, and_123_out);
  Delay #(.delayTime(3)) delay_10 (.in(and_128_out), .out(delay_10_out));
  and and_129 (Clear, not_29_out, delay_9_out);
  not not_33 (not_33_out, or_59_out);
  and and_130 (and_130_out, not_33_out, delay_7_out);
  BCD_Gate bcd_gate_4 (
    .B_1(bcd_gate_2_o_4), .B_2(bcd_gate_5_o_1), .B_3(bcd_gate_5_o_2), .B_4(bcd_gate_5_o_3), .O_1(Tens[1]),
    .O_2(Tens[2]), .O_3(Tens[3]), .O_4(Hundreds[0]));
  BCD_Gate bcd_gate_5 (
    .B_1(bcd_gate_3_o_4), .B_2(bcd_gate_6_o_1), .B_3(bcd_gate_6_o_2), .B_4(bcd_gate_6_o_3),
    .O_1(bcd_gate_5_o_1), .O_2(bcd_gate_5_o_2), .O_3(bcd_gate_5_o_3), .O_4(bcd_gate_5_o_4));
  BCD_Gate bcd_gate_6 (
    .B_1(bcd_gate_7_o_4), .B_2(bcd_gate_14_o_1), .B_3(bcd_gate_14_o_2), .B_4(bcd_gate_14_o_3),
    .O_1(bcd_gate_6_o_1), .O_2(bcd_gate_6_o_2), .O_3(bcd_gate_6_o_3), .O_4(bcd_gate_6_o_4));
  BCD_Gate bcd_gate_7 (
    .B_1(multiplexer_4_out[4]), .B_2(bcd_gate_8_o_1), .B_3(bcd_gate_8_o_2), .B_4(bcd_gate_8_o_3),
    .O_1(bcd_gate_7_o_1), .O_2(bcd_gate_7_o_2), .O_3(bcd_gate_7_o_3), .O_4(bcd_gate_7_o_4));
  BCD_Gate bcd_gate_8 (
    .B_1(multiplexer_4_out[5]), .B_2(bcd_gate_9_o_1), .B_3(bcd_gate_9_o_2), .B_4(bcd_gate_9_o_3),
    .O_1(bcd_gate_8_o_1), .O_2(bcd_gate_8_o_2), .O_3(bcd_gate_8_o_3), .O_4(bcd_gate_8_o_4));
  BCD_Gate bcd_gate_9 (
    .B_1(multiplexer_4_out[6]), .B_2(bcd_gate_10_o_1), .B_3(bcd_gate_10_o_2), .B_4(bcd_gate_10_o_3),
    .O_1(bcd_gate_9_o_1), .O_2(bcd_gate_9_o_2), .O_3(bcd_gate_9_o_3), .O_4(bcd_gate_9_o_4));
  BCD_Gate bcd_gate_10 (
    .B_1(multiplexer_4_out[7]), .B_2(bcd_gate_18_o_1), .B_3(bcd_gate_18_o_2), .B_4(bcd_gate_18_o_3),
    .O_1(bcd_gate_10_o_1), .O_2(bcd_gate_10_o_2), .O_3(bcd_gate_10_o_3), .O_4(bcd_gate_10_o_4));
  or or_61 (or_61_out, 1'b0, Binary_1[0], Binary_1[1], Binary_1[2], Binary_1[3], 1'b0, 1'b0, 1'b0, 1'b0, 1'b0, 1'b0, 1'b0, 1'b0, 1'b0, 1'b0, 1'b0);
  or or_62 (or_62_out, and_142_out, or_61_out);
  and and_131 (and_131_out, not_30_out, delay_10_out);
  not not_34 (not_34_out, or_60_out);
  BCD_Gate bcd_gate_11 (
    .B_1(bcd_gate_5_o_4), .B_2(bcd_gate_12_o_1), .B_3(bcd_gate_12_o_2), .B_4(bcd_gate_12_o_3),
    .O_1(Hundreds[1]), .O_2(Hundreds[2]), .O_3(Hundreds[3]), .O_4(Thousands[0]));
  BCD_Gate bcd_gate_12 (
    .B_1(bcd_gate_6_o_4), .B_2(bcd_gate_13_o_1), .B_3(bcd_gate_13_o_2), .B_4(bcd_gate_13_o_3),
    .O_1(bcd_gate_12_o_1), .O_2(bcd_gate_12_o_2), .O_3(bcd_gate_12_o_3), .O_4(bcd_gate_12_o_4));
  BCD_Gate bcd_gate_13 (
    .B_1(bcd_gate_14_o_4), .B_2(bcd_gate_25_o_1), .B_3(bcd_gate_25_o_2), .B_4(bcd_gate_25_o_3),
    .O_1(bcd_gate_13_o_1), .O_2(bcd_gate_13_o_2), .O_3(bcd_gate_13_o_3), .O_4(bcd_gate_13_o_4));
  BCD_Gate bcd_gate_14 (
    .B_1(bcd_gate_8_o_4), .B_2(bcd_gate_15_o_1), .B_3(bcd_gate_15_o_2), .B_4(bcd_gate_15_o_3),
    .O_1(bcd_gate_14_o_1), .O_2(bcd_gate_14_o_2), .O_3(bcd_gate_14_o_3), .O_4(bcd_gate_14_o_4));
  BCD_Gate bcd_gate_15 (
    .B_1(bcd_gate_9_o_4), .B_2(bcd_gate_16_o_1), .B_3(bcd_gate_16_o_2), .B_4(bcd_gate_16_o_3),
    .O_1(bcd_gate_15_o_1), .O_2(bcd_gate_15_o_2), .O_3(bcd_gate_15_o_3), .O_4(bcd_gate_15_o_4));
  BCD_Gate bcd_gate_16 (
    .B_1(bcd_gate_10_o_4), .B_2(bcd_gate_17_o_1), .B_3(bcd_gate_17_o_2), .B_4(bcd_gate_17_o_3),
    .O_1(bcd_gate_16_o_1), .O_2(bcd_gate_16_o_2), .O_3(bcd_gate_16_o_3), .O_4(bcd_gate_16_o_4));
  BCD_Gate bcd_gate_17 (
    .B_1(bcd_gate_18_o_4), .B_2(bcd_gate_29_o_1), .B_3(bcd_gate_29_o_2), .B_4(bcd_gate_29_o_3),
    .O_1(bcd_gate_17_o_1), .O_2(bcd_gate_17_o_2), .O_3(bcd_gate_17_o_3), .O_4(bcd_gate_17_o_4));
  BCD_Gate bcd_gate_18 (
    .B_1(multiplexer_4_out[8]), .B_2(bcd_gate_19_o_1), .B_3(bcd_gate_19_o_2), .B_4(bcd_gate_19_o_3),
    .O_1(bcd_gate_18_o_1), .O_2(bcd_gate_18_o_2), .O_3(bcd_gate_18_o_3), .O_4(bcd_gate_18_o_4));
  BCD_Gate bcd_gate_19 (
    .B_1(multiplexer_4_out[9]), .B_2(bcd_gate_20_o_1), .B_3(bcd_gate_20_o_2), .B_4(bcd_gate_20_o_3),
    .O_1(bcd_gate_19_o_1), .O_2(bcd_gate_19_o_2), .O_3(bcd_gate_19_o_3), .O_4(bcd_gate_19_o_4));
  BCD_Gate bcd_gate_20 (
    .B_1(multiplexer_4_out[10]), .B_2(bcd_gate_21_o_1), .B_3(bcd_gate_21_o_2), .B_4(bcd_gate_21_o_3),
    .O_1(bcd_gate_20_o_1), .O_2(bcd_gate_20_o_2), .O_3(bcd_gate_20_o_3), .O_4(bcd_gate_20_o_4));
  BCD_Gate bcd_gate_21 (
    .B_1(multiplexer_4_out[11]), .B_2(bcd_gate_33_o_1), .B_3(bcd_gate_33_o_2), .B_4(bcd_gate_33_o_3),
    .O_1(bcd_gate_21_o_1), .O_2(bcd_gate_21_o_2), .O_3(bcd_gate_21_o_3), .O_4(bcd_gate_21_o_4));
  not not_35 (not_35_out, and_127_out);
  and and_132 (and_132_out, not_35_out, not_32_out);
  and and_133 (and_133_out, and_131_out, Cycle_1);
  and and_134 (and_134_out, not_34_out, delay_8_out);
  and and_135 (and_135_out, and_134_out, Cycle_1);
  and and_136 (and_136_out, Clear, Cycle_1);
  and and_137 (and_137_out, and_130_out, Cycle_1);
  BCD_Gate bcd_gate_22 (
    .B_1(bcd_gate_12_o_4), .B_2(bcd_gate_23_o_1), .B_3(bcd_gate_23_o_2), .B_4(bcd_gate_23_o_3),
    .O_1(Thousands[1]), .O_2(Thousands[2]), .O_3(Thousands[3]), .O_4(Tens_of_Thousands[0]));
  BCD_Gate bcd_gate_23 (
    .B_1(bcd_gate_13_o_4), .B_2(bcd_gate_24_o_1), .B_3(bcd_gate_24_o_2), .B_4(bcd_gate_24_o_3),
    .O_1(bcd_gate_23_o_1), .O_2(bcd_gate_23_o_2), .O_3(bcd_gate_23_o_3), .O_4(bcd_gate_23_o_4));
  BCD_Gate bcd_gate_24 (
    .B_1(bcd_gate_25_o_4), .B_2(bcd_gate_38_o_1), .B_3(bcd_gate_38_o_2), .B_4(bcd_gate_38_o_3),
    .O_1(bcd_gate_24_o_1), .O_2(bcd_gate_24_o_2), .O_3(bcd_gate_24_o_3), .O_4(bcd_gate_24_o_4));
  BCD_Gate bcd_gate_25 (
    .B_1(bcd_gate_15_o_4), .B_2(bcd_gate_26_o_1), .B_3(bcd_gate_26_o_2), .B_4(bcd_gate_26_o_3),
    .O_1(bcd_gate_25_o_1), .O_2(bcd_gate_25_o_2), .O_3(bcd_gate_25_o_3), .O_4(bcd_gate_25_o_4));
  BCD_Gate bcd_gate_26 (
    .B_1(bcd_gate_16_o_4), .B_2(bcd_gate_27_o_1), .B_3(bcd_gate_27_o_2), .B_4(bcd_gate_27_o_3),
    .O_1(bcd_gate_26_o_1), .O_2(bcd_gate_26_o_2), .O_3(bcd_gate_26_o_3), .O_4(bcd_gate_26_o_4));
  BCD_Gate bcd_gate_27 (
    .B_1(bcd_gate_17_o_4), .B_2(bcd_gate_28_o_1), .B_3(bcd_gate_28_o_2), .B_4(bcd_gate_28_o_3),
    .O_1(bcd_gate_27_o_1), .O_2(bcd_gate_27_o_2), .O_3(bcd_gate_27_o_3), .O_4(bcd_gate_27_o_4));
  BCD_Gate bcd_gate_28 (
    .B_1(bcd_gate_29_o_4), .B_2(bcd_gate_40_o_1), .B_3(bcd_gate_40_o_2), .B_4(bcd_gate_40_o_3),
    .O_1(bcd_gate_28_o_1), .O_2(bcd_gate_28_o_2), .O_3(bcd_gate_28_o_3), .O_4(bcd_gate_28_o_4));
  BCD_Gate bcd_gate_29 (
    .B_1(bcd_gate_19_o_4), .B_2(bcd_gate_30_o_1), .B_3(bcd_gate_30_o_2), .B_4(bcd_gate_30_o_3),
    .O_1(bcd_gate_29_o_1), .O_2(bcd_gate_29_o_2), .O_3(bcd_gate_29_o_3), .O_4(bcd_gate_29_o_4));
  BCD_Gate bcd_gate_30 (
    .B_1(bcd_gate_20_o_4), .B_2(bcd_gate_31_o_1), .B_3(bcd_gate_31_o_2), .B_4(bcd_gate_31_o_3),
    .O_1(bcd_gate_30_o_1), .O_2(bcd_gate_30_o_2), .O_3(bcd_gate_30_o_3), .O_4(bcd_gate_30_o_4));
  BCD_Gate bcd_gate_31 (
    .B_1(bcd_gate_21_o_4), .B_2(bcd_gate_32_o_1), .B_3(bcd_gate_32_o_2), .B_4(bcd_gate_32_o_3),
    .O_1(bcd_gate_31_o_1), .O_2(bcd_gate_31_o_2), .O_3(bcd_gate_31_o_3), .O_4(bcd_gate_31_o_4));
  BCD_Gate bcd_gate_32 (
    .B_1(bcd_gate_33_o_4), .B_2(bcd_gate_34_o_4), .B_3(bcd_gate_35_o_4), .B_4(pulldown_20_out),
    .O_1(bcd_gate_32_o_1), .O_2(bcd_gate_32_o_2), .O_3(bcd_gate_32_o_3), .O_4(bcd_gate_32_o_4));
  BCD_Gate bcd_gate_33 (
    .B_1(multiplexer_4_out[12]), .B_2(bcd_gate_34_o_1), .B_3(bcd_gate_34_o_2), .B_4(bcd_gate_34_o_3),
    .O_1(bcd_gate_33_o_1), .O_2(bcd_gate_33_o_2), .O_3(bcd_gate_33_o_3), .O_4(bcd_gate_33_o_4));
  BCD_Gate bcd_gate_34 (
    .B_1(multiplexer_4_out[13]), .B_2(bcd_gate_35_o_1), .B_3(bcd_gate_35_o_2), .B_4(bcd_gate_35_o_3),
    .O_1(bcd_gate_34_o_1), .O_2(bcd_gate_34_o_2), .O_3(bcd_gate_34_o_3), .O_4(bcd_gate_34_o_4));
  BCD_Gate bcd_gate_35 (
    .B_1(multiplexer_4_out[14]), .B_2(multiplexer_4_out[15]), .B_3(pulldown_22_out), .B_4(pulldown_19_out),
    .O_1(bcd_gate_35_o_1), .O_2(bcd_gate_35_o_2), .O_3(bcd_gate_35_o_3), .O_4(bcd_gate_35_o_4));
  xor xor_3 (xor_3_out, and_127_out, 1'b0);
  and and_138 (and_138_out, and_126_out, and_122_out);
  and and_139 (and_139_out, Cycle_1, or_62_out);
  DiodeForward diodeforward_46 (.in(and_134_out), .out(diodeforward_46_out));
  BCD_Gate bcd_gate_36 (
    .B_1(bcd_gate_23_o_4), .B_2(bcd_gate_37_o_1), .B_3(bcd_gate_37_o_2), .B_4(bcd_gate_37_o_3),
    .O_1(Tens_of_Thousands[1]), .O_2(Tens_of_Thousands[2]), .O_3(Tens_of_Thousands[3]),
    .O_4(Hundreds__of_Thousands[0]));
  BCD_Gate bcd_gate_37 (
    .B_1(bcd_gate_24_o_4), .B_2(bcd_gate_38_o_4), .B_3(bcd_gate_39_o_4), .B_4(pulldown_25_out),
    .O_1(bcd_gate_37_o_1), .O_2(bcd_gate_37_o_2), .O_3(bcd_gate_37_o_3), .O_4(bcd_gate_37_o_4));
  BCD_Gate bcd_gate_38 (
    .B_1(bcd_gate_26_o_4), .B_2(bcd_gate_39_o_1), .B_3(bcd_gate_39_o_2), .B_4(bcd_gate_39_o_3),
    .O_1(bcd_gate_38_o_1), .O_2(bcd_gate_38_o_2), .O_3(bcd_gate_38_o_3), .O_4(bcd_gate_38_o_4));
  BCD_Gate bcd_gate_39 (
    .B_1(bcd_gate_27_o_4), .B_2(bcd_gate_28_o_4), .B_3(bcd_gate_40_o_4), .B_4(pulldown_24_out),
    .O_1(bcd_gate_39_o_1), .O_2(bcd_gate_39_o_2), .O_3(bcd_gate_39_o_3), .O_4(bcd_gate_39_o_4));
  BCD_Gate bcd_gate_40 (
    .B_1(bcd_gate_30_o_4), .B_2(bcd_gate_31_o_4), .B_3(bcd_gate_32_o_4), .B_4(pulldown_21_out),
    .O_1(bcd_gate_40_o_1), .O_2(bcd_gate_40_o_2), .O_3(bcd_gate_40_o_3), .O_4(bcd_gate_40_o_4));
  PullDown pulldown_19 (.out(pulldown_19_out));
  PullDown pulldown_20 (.out(pulldown_20_out));
  PullDown pulldown_21 (.out(pulldown_21_out));
  PullDown pulldown_22 (.out(pulldown_22_out));
  and and_140 (and_140_out, and_127_out, 1'b0);
  DiodeForward diodeforward_47 (.in(and_133_out), .out(Operator_Pressed));
  PullDown pulldown_23 (.out(diodeforward_46_out));
  DiodeForward diodeforward_48 (.in(and_135_out), .out(Operator_Pressed));
  DiodeForward diodeforward_49 (.in(and_136_out), .out(Operator_Pressed));
  DiodeForward diodeforward_50 (.in(and_137_out), .out(Operator_Pressed));
  BCD_Gate bcd_gate_41 (
    .B_1(bcd_gate_37_o_4), .B_2(pulldown_26_out), .B_3(pulldown_27_out), .B_4(pulldown_28_out),
    .O_1(Hundreds__of_Thousands[1]), .O_2(Hundreds__of_Thousands[2]), .O_3(Hundreds__of_Thousands[3]));  // open: O_4
  PullDown pulldown_24 (.out(pulldown_24_out));
  PullDown pulldown_25 (.out(pulldown_25_out));
  PullDown pulldown_26 (.out(pulldown_26_out));
  PullDown pulldown_27 (.out(pulldown_27_out));
  xor xor_4 (Binary_1[0], 1'b0, xor_3_out);
  and and_141 (and_141_out, xor_3_out, 1'b0);
  and and_142 (and_142_out, and_138_out, and_132_out);
  not not_36 (not_36_out, Operator_Pressed);
  PullDown pulldown_28 (.out(pulldown_28_out));
  or or_63 (or_63_out, and_140_out, and_141_out);
  and and_143 (Cycle_2, and_139_out, not_36_out);
  Multiplexer multiplexer_5 (.sel(not_37_out), .in_0(1'b0), .in_1(and_131_out), .out(multiplexer_5_out));
  Multiplexer multiplexer_6 (.sel(not_37_out), .in_0(1'b0), .in_1(diodeforward_46_out), .out(multiplexer_6_out));
  Delay #(.delayTime(5)) delay_11 (.in(Clear), .out(delay_11_out));
  not not_37 (not_37_out, delay_11_out);
  Multiplexer multiplexer_7 (.sel(not_37_out), .in_0(1'b0), .in_1(and_130_out), .out(Equal));
  DiodeForward diodeforward_51 (.in(multiplexer_6_out), .out(Add));
  PullDown pulldown_29 (.out(Operator_Pressed));
  Multiplexer #(.Bits(16)) multiplexer_8 (.sel(or_65_out), .in_0(Reg_A_In), .in_1({16{1'b0}}), .out(T1));
  Delay #(.delayTime(10)) delay_12 (.in(multiplexer_5_out), .out(Sub_process));
  PullDown pulldown_30 (.out(Add));
  DiodeForward diodeforward_52 (.in(Equal), .out(Add));
  or or_64 (or_64_out, Shift_Cycle, ALU_Cycle);
  and and_144 (and_144_out, ALU_Cycle, or_65_out);
  xor xor_5 (xor_5_out, InputA1, InputB1);
  and and_145 (and_145_out, InputA1, InputB1);
  xor xor_6 (xor_6_out, InputA2, InputB2);
  and and_146 (and_146_out, InputA2, InputB2);
  xor xor_7 (xor_7_out, InputA3, InputB3);
  and and_147 (and_147_out, InputA3, InputB3);
  xor xor_8 (xor_8_out, InputA4, InputB4);
  and and_148 (and_148_out, InputA4, InputB4);
  xor xor_9 (xor_9_out, InputA5, InputB5);
  and and_149 (and_149_out, InputA5, InputB5);
  xor xor_10 (xor_10_out, InputA6, InputB6);
  and and_150 (and_150_out, InputA6, InputB6);
  xor xor_11 (xor_11_out, InputA7, InputB7);
  and and_151 (and_151_out, InputA7, InputB7);
  xor xor_12 (xor_12_out, InputA8, InputB8);
  and and_152 (and_152_out, InputA8, InputB8);
  xor xor_13 (xor_13_out, and_126_out, 1'b0);
  and and_153 (and_153_out, and_126_out, 1'b0);
  or or_65 (or_65_out, Add, Sub);
  xor xor_14 (xor_14_out, or_63_out, xor_13_out);
  and and_154 (and_154_out, xor_13_out, or_63_out);
  Multiplexer #(.Selector_Bits(3), .Bits(16)) multiplexer_9 (
    .sel(ALU_MUX), .in_0(out_1), .in_1(pulldown_31_out), .in_2(not_38_out), .in_3(out_3),
    .in_4({out_1[12:0], 3'b000}), .in_5(_10x_BIN), .in_6(pulldown_34_out), .in_7(pulldown_34_out),
    .out({InputA16, InputA15, InputA14, InputA13, InputA12, InputA11, InputA10, InputA9, InputA8, InputA7, InputA6, InputA5, InputA4, InputA3, InputA2, InputA1}));
  DiodeForward diodeforward_53 (.in(or_64_out), .out(diodeforward_53_out));
  DiodeForward diodeforward_54 (.in(delay_13_out), .out(diodeforward_54_out));
  Delay #(.delayTime(4)) delay_13 (.in(and_144_out), .out(delay_13_out));
  xor xor_15 (xor_19_out[0], 1'b0, xor_5_out);
  and and_155 (and_155_out, xor_5_out, 1'b0);
  xor xor_16 (xor_19_out[1], Carry1, xor_6_out);
  and and_156 (and_156_out, xor_6_out, Carry1);
  xor xor_17 (xor_19_out[2], Carry2, xor_7_out);
  and and_157 (and_157_out, xor_7_out, Carry2);
  xor xor_18 (xor_19_out[3], Carry3, xor_8_out);
  and and_158 (and_158_out, xor_8_out, Carry3);
  xor xor_19 (xor_19_out[4], Carry4, xor_9_out);
  and and_159 (and_159_out, xor_9_out, Carry4);
  xor xor_20 (xor_19_out[5], Carry5, xor_10_out);
  and and_160 (and_160_out, xor_10_out, Carry5);
  xor xor_21 (xor_19_out[6], Carry6, xor_11_out);
  and and_161 (and_161_out, xor_11_out, Carry6);
  xor xor_22 (xor_19_out[7], Carry7, xor_12_out);
  and and_162 (and_162_out, xor_12_out, Carry7);
  PullDown #(.Bits(16)) pulldown_31 (.out(pulldown_31_out));
  assign not_38_out = ~out_1;  // Not not_38, 16 bits wide
  Multiplexer #(.Bits(16)) multiplexer_10 (.sel(Clear), .in_0(ALU_B), .in_1({16{1'b0}}), .out(multiplexer_10_out));
  PullDown pulldown_32 (.out(diodeforward_54_out));
  or or_66 (Carry1, and_145_out, and_155_out);
  or or_67 (Carry2, and_146_out, and_156_out);
  or or_68 (Carry3, and_147_out, and_157_out);
  or or_69 (Carry4, and_148_out, and_158_out);
  or or_70 (Carry5, and_149_out, and_159_out);
  or or_71 (Carry6, and_150_out, and_160_out);
  or or_72 (Carry7, and_151_out, and_161_out);
  or or_73 (Carry8, and_152_out, and_162_out);
  or or_74 (or_74_out, and_153_out, and_154_out);
  PullDown pulldown_33 (.out(diodeforward_53_out));
  Delay #(.delayTime(20)) delay_14 (.in(Cycle_1), .out(Cycle_3));
  PullDown #(.Bits(16)) pulldown_34 (.out(pulldown_34_out));
  Multiplexer #(.Bits(16)) multiplexer_11 (.sel(Clear), .in_0(T1), .in_1({16{1'b0}}), .out(multiplexer_11_out));
  xor xor_23 (xor_23_out, and_123_out, 1'b0);
  and and_163 (and_163_out, and_123_out, 1'b0);
  Multiplexer #(.Selector_Bits(3), .Bits(16)) multiplexer_12 (
    .sel(ALU_MUX), .in_0(out_2), .in_1(pulldown_36_out), .in_2(16'h1), .in_3(out_2),
    .in_4({out_1[14:0], 1'b0}), .in_5({{12{1'b0}}, Binary_1}), .in_6(pulldown_39_out),
    .in_7(pulldown_39_out),
    .out({InputB16, InputB15, InputB14, InputB13, InputB12, InputB11, InputB10, InputB9, InputB8, InputB7, InputB6, InputB5, InputB4, InputB3, InputB2, InputB1}));
  DiodeForward diodeforward_55 (.in(diodeforward_53_out), .out(diodeforward_55_out));
  DiodeForward diodeforward_56 (.in(Clear), .out(diodeforward_55_out));
  DiodeForward diodeforward_57 (.in(Clear), .out(diodeforward_54_out));
  PullDown #(.Bits(16)) pulldown_35 (.out(pulldown_35_out));
  Demultiplexer #(.Selector_Bits(3), .Bits(16)) demultiplexer_1 (
    .sel(ALU_MUX), .in({Output_9_16, xor_19_out}), .out_0(S), .out_1(pulldown_35_out), .out_2(Temp_in),
    .out_3(subtracted), .out_4(Sum_3), .out_5(sum_4));  // open: out_6, out_7
  xor xor_24 (Binary_1[2], or_74_out, xor_23_out);
  and and_164 (and_164_out, xor_23_out, or_74_out);
  PullDown #(.Bits(16)) pulldown_36 (.out(pulldown_36_out));
  Register #(.Bits(16)) Reg_A (.D(multiplexer_11_out), .C(diodeforward_55_out), .en(Cycle_1), .Q(out_1));
  PullDown pulldown_37 (.out(diodeforward_55_out));
  PullDown pulldown_38 (.out(diodeforward_54_out));
  Register #(.Bits(16)) Reg_B (.D(multiplexer_10_out), .C(diodeforward_54_out), .en(Cycle_1), .Q(out_2));
  or or_75 (or_75_out, and_163_out, and_164_out);
  PullDown #(.Bits(16)) pulldown_39 (.out(pulldown_39_out));
  Delay #(.delayTime(20)) delay_15 (.in(delay_17_out), .out(delay_15_out));
  Delay #(.delayTime(20)) delay_16 (.in(delay_15_out), .out(delay_16_out));
  Delay #(.delayTime(20)) delay_17 (.in(delay_20_out), .out(delay_17_out));
  Delay #(.delayTime(20)) delay_18 (.in(delay_16_out), .out(delay_18_out));
  xor xor_25 (xor_25_out, and_122_out, 1'b0);
  and and_165 (and_165_out, and_122_out, 1'b0);
  Delay #(.delayTime(2)) delay_19 (.in(Add), .out(delay_19_out));
  Delay #(.delayTime(20)) delay_20 (.in(delay_23_out), .out(delay_20_out));
  Delay #(.delayTime(20)) delay_21 (.in(delay_18_out), .out(delay_21_out));
  xor xor_26 (xor_26_out, InputA9, InputB9);
  and and_166 (and_166_out, InputA9, InputB9);
  xor xor_27 (xor_27_out, InputA10, InputB10);
  and and_167 (and_167_out, InputA10, InputB10);
  xor xor_28 (xor_28_out, InputA11, InputB11);
  and and_168 (and_168_out, InputA11, InputB11);
  xor xor_29 (xor_29_out, InputA12, InputB12);
  and and_169 (and_169_out, InputA12, InputB12);
  xor xor_30 (xor_30_out, InputA13, InputB13);
  and and_170 (and_170_out, InputA13, InputB13);
  xor xor_31 (xor_31_out, InputA14, InputB14);
  and and_171 (and_171_out, InputA14, InputB14);
  xor xor_32 (xor_32_out, InputA15, InputB15);
  and and_172 (and_172_out, InputA15, InputB15);
  xor xor_33 (xor_33_out, InputA16, InputB16);
  and and_173 (and_173_out, InputA16, InputB16);
  xor xor_34 (xor_34_out, or_75_out, xor_25_out);
  and and_174 (and_174_out, xor_25_out, or_75_out);
  Multiplexer #(.Bits(16)) multiplexer_13 (.sel(delay_19_out), .in_0({16{1'b0}}), .in_1(S), .out(multiplexer_13_out));
  DiodeForward diodeforward_58 (.in(delay_19_out), .out(diodeforward_58_out));
  Multiplexer #(.Bits(16)) multiplexer_14 (.sel(Sub), .in_0({16{1'b0}}), .in_1(subtracted), .out(multiplexer_14_out));
  DiodeForward diodeforward_59 (.in(Sub), .out(diodeforward_58_out));
  Delay #(.delayTime(20)) delay_22 (.in(Sub_process), .out(delay_22_out));
  Delay #(.delayTime(20)) delay_23 (.in(delay_22_out), .out(delay_23_out));
  Delay #(.delayTime(20)) delay_24 (.in(delay_21_out), .out(delay_24_out));
  xor xor_35 (Output_9_16[0], Carry8, xor_26_out);
  xor xor_36 (Output_9_16[1], Carry9, xor_27_out);
  xor xor_37 (Output_9_16[2], Carry10, xor_28_out);
  xor xor_38 (Output_9_16[3], Carry11, xor_29_out);
  xor xor_39 (Output_9_16[4], Carry12, xor_30_out);
  xor xor_40 (Output_9_16[5], Carry13, xor_31_out);
  xor xor_41 (Output_9_16[6], Carry14, xor_32_out);
  xor xor_42 (Output_9_16[7], Carry15, xor_33_out);
  assign ALU_B = multiplexer_13_out | multiplexer_14_out;  // Or or_76, 16 bits wide
  PullDown pulldown_40 (.out(diodeforward_58_out));
  and and_175 (and_175_out, Cycle_1, diodeforward_58_out);
  Delay #(.delayTime(20)) delay_25 (.in(delay_24_out), .out(delay_25_out));
  and and_176 (and_176_out, xor_26_out, Carry8);
  and and_177 (and_177_out, xor_27_out, Carry9);
  and and_178 (and_178_out, xor_28_out, Carry10);
  and and_179 (and_179_out, xor_29_out, Carry11);
  and and_180 (and_180_out, xor_30_out, Carry12);
  and and_181 (and_181_out, xor_31_out, Carry13);
  and and_182 (and_182_out, xor_32_out, Carry14);
  and and_183 (and_183_out, xor_33_out, Carry15);
  // Or or_77 has open pins: In_1=and_165_out, In_2=and_174_out, out=open
  Delay #(.delayTime(20)) delay_26 (.in(delay_31_out), .out(delay_26_out));
  Delay #(.delayTime(20)) delay_27 (.in(and_175_out), .out(delay_27_out));
  Delay #(.delayTime(20)) delay_28 (.in(Sub_process), .out(delay_28_out));
  Delay #(.delayTime(20)) delay_29 (.in(delay_28_out), .out(delay_29_out));
  RS_FF_AS rs_ff_as_4 (.S(Sub_process), .R(delay_25_out), .Q(rs_ff_as_4_q));  // open: nQ
  or or_78 (Carry9, and_166_out, and_176_out);
  or or_79 (Carry10, and_167_out, and_177_out);
  or or_80 (Carry11, and_168_out, and_178_out);
  or or_81 (Carry12, and_169_out, and_179_out);
  or or_82 (Carry13, and_170_out, and_180_out);
  or or_83 (Carry14, and_171_out, and_181_out);
  or or_84 (Carry15, and_172_out, and_182_out);
  or or_85 (or_85_out, and_173_out, and_183_out);
  Delay #(.delayTime(20)) delay_30 (.in(delay_26_out), .out(delay_30_out));
  Delay #(.delayTime(20)) delay_31 (.in(delay_27_out), .out(delay_31_out));
  Delay #(.delayTime(20)) delay_32 (.in(delay_30_out), .out(delay_32_out));
  Delay #(.delayTime(10)) delay_33 (.in(delay_29_out), .out(delay_33_out));
  DiodeForward diodeforward_60 (.in(rs_ff_as_4_q), .out(ALU_MUX[1]));
  PullDown pulldown_41 (.out(or_85_out));
  xor xor_43 (Binary_1[1], and_142_out, xor_14_out);
  xor xor_44 (Binary_1[3], xor_34_out, and_142_out);
  Delay #(.delayTime(20)) delay_34 (.in(delay_32_out), .out(ALU_Cycle));
  Register #(.Bits(16)) Sub_Register (.D(Temp_in), .C(delay_33_out), .en(Cycle_1), .Q(out_3));
  Delay #(.delayTime(20)) delay_35 (.in(delay_36_out), .out(delay_35_out));
  Delay #(.delayTime(20)) delay_36 (.in(rs_ff_as_4_q), .out(delay_36_out));
  Delay #(.delayTime(20)) delay_37 (.in(delay_35_out), .out(delay_37_out));
  RS_FF_AS rs_ff_as_5 (.S(delay_37_out), .R(delay_25_out), .Q(Sub));  // open: nQ
  DiodeForward diodeforward_61 (.in(Sub), .out(ALU_MUX[0]));
  DiodeForward diodeforward_62 (.in(Cycle_2), .out(ALU_MUX[2]));
  PullDown pulldown_42 (.out(ALU_MUX[1]));
  PullDown pulldown_43 (.out(ALU_MUX[0]));
  PullDown pulldown_44 (.out(ALU_MUX[2]));
  DiodeForward diodeforward_63 (.in(cycle_2_5), .out(ALU_MUX[0]));

  // Other names for the same wires on the sheet: C_Bin[3:0] = Binary_1; MUX_1 = ALU_MUX[1]; A[15:0] = out_1;
  //   Inverter[15:0] = out_1; Reg_A_Out[15:0] = out_1; Sum_1[15:3] = out_1[12:0]; Sum_2[15:1] = out_1[14:0];
  //   B[15:0] = out_2; Reg_B_Out[15:0] = out_2; Reg_cycle = Cycle_1; Temp_out[15:0] = out_3

  // Notes on the sheet:
  //   00001 - 1
  //   00010 - 2
  //   00011 - 3
  //   00100 - 4
  //   00101 - 5
  //   00110 - 6
  //   00111 - 7
  //   01000 - 8
  //   01001 - 9
  //   01010 - 0
  //   11000 - =
  //   10000 - +
  //   10100 - -
  //   11100 - CLR
  //   0000 0000 = OFF
  //   1111 1100 = 0
  //   0110 0000 = 1
  //   1101 1010 = 2
  //   1111 0010 = 3
  //   0110 0110 = 4
  //   1011 0110 = 5
  //   1011 1110 = 6
  //   1110 0000 = 7
  //   1111 1110 = 8
  //   1110 0110 = 9
endmodule
