// Digital circuit 8 bit Ben Eater Register.dig as structural Verilog
module _8_bit_Ben_Eater_Register (
  input  Load,
  input  D1,
  input  D2,
  input  clk,
  input  D3,
  input  D4,
  input  D5,
  input  D6,
  input  D7,
  input  D8,
  input  Enable,
  output O1,
  output O2,
  output O3,
  output O4,
  output O5,
  output O6,
  output O7,
  output O8
);

  wire and_1_out, and_2_out, and_3_out, and_4_out, and_5_out, and_6_out, and_7_out, and_8_out, and_9_out,
       and_10_out, and_11_out, and_12_out, and_13_out, and_14_out, and_15_out, and_16_out, d_ff_1_q,
       d_ff_2_q, d_ff_3_q, d_ff_4_q, d_ff_5_q, d_ff_6_q, d_ff_7_q, d_ff_8_q, not_1_out, not_2_out, not_3_out,
       not_4_out, not_5_out, not_6_out, not_7_out, not_8_out, or_1_out, or_2_out, or_3_out, or_4_out,
       or_5_out, or_6_out, or_7_out, or_8_out;

  not not_1 (not_1_out, Load);
  not not_2 (not_2_out, Load);
  not not_3 (not_3_out, Load);
  not not_4 (not_4_out, Load);
  not not_5 (not_5_out, Load);
  not not_6 (not_6_out, Load);
  not not_7 (not_7_out, Load);
  not not_8 (not_8_out, Load);
  and and_1 (and_1_out, d_ff_1_q, not_1_out);
  and and_2 (and_2_out, Load, D1);
  and and_3 (and_3_out, d_ff_2_q, not_2_out);
  and and_4 (and_4_out, Load, D2);
  and and_5 (and_5_out, d_ff_3_q, not_3_out);
  and and_6 (and_6_out, Load, D3);
  and and_7 (and_7_out, d_ff_4_q, not_4_out);
  and and_8 (and_8_out, Load, D4);
  and and_9 (and_9_out, d_ff_5_q, not_5_out);
  and and_10 (and_10_out, Load, D5);
  and and_11 (and_11_out, d_ff_6_q, not_6_out);
  and and_12 (and_12_out, Load, D6);
  and and_13 (and_13_out, d_ff_7_q, not_7_out);
  and and_14 (and_14_out, Load, D7);
  and and_15 (and_15_out, d_ff_8_q, not_8_out);
  and and_16 (and_16_out, Load, D8);
  or or_1 (or_1_out, and_1_out, and_2_out);
  or or_2 (or_2_out, and_3_out, and_4_out);
  or or_3 (or_3_out, and_5_out, and_6_out);
  or or_4 (or_4_out, and_7_out, and_8_out);
  or or_5 (or_5_out, and_9_out, and_10_out);
  or or_6 (or_6_out, and_11_out, and_12_out);
  or or_7 (or_7_out, and_13_out, and_14_out);
  or or_8 (or_8_out, and_15_out, and_16_out);
  D_FF d_ff_1 (.D(or_1_out), .C(clk), .Q(d_ff_1_q));  // open: nQ
  D_FF d_ff_2 (.D(or_2_out), .C(clk), .Q(d_ff_2_q));  // open: nQ
  D_FF d_ff_3 (.D(or_3_out), .C(clk), .Q(d_ff_3_q));  // open: nQ
  D_FF d_ff_4 (.D(or_4_out), .C(clk), .Q(d_ff_4_q));  // open: nQ
  D_FF d_ff_5 (.D(or_5_out), .C(clk), .Q(d_ff_5_q));  // open: nQ
  D_FF d_ff_6 (.D(or_6_out), .C(clk), .Q(d_ff_6_q));  // open: nQ
  D_FF d_ff_7 (.D(or_7_out), .C(clk), .Q(d_ff_7_q));  // open: nQ
  D_FF d_ff_8 (.D(or_8_out), .C(clk), .Q(d_ff_8_q));  // open: nQ
  and and_17 (O1, Enable, d_ff_1_q);
  and and_18 (O2, d_ff_2_q, Enable);
  and and_19 (O3, d_ff_3_q, Enable);
  and and_20 (O4, d_ff_4_q, Enable);
  and and_21 (O5, d_ff_5_q, Enable);
  and and_22 (O6, d_ff_6_q, Enable);
  and and_23 (O7, d_ff_7_q, Enable);
  and and_24 (O8, d_ff_8_q, Enable);

  // Notes on the sheet:
  //   clk: Hz: 3
endmodule
