// Digital circuit 8bit register 74173 74245.dig as structural Verilog
module _8bit_register_74173_74245 (
  input  VCC,
  input  GND,
  input  CLR,
  input  CLK,
  input  Load,
  input  Enable,
  input  D1,
  input  D2,
  input  D3,
  input  D4,
  input  D5,
  input  D6,
  input  D7,
  input  D8,
  output O1,
  output O2,
  output O3,
  output O4,
  output O5,
  output O6,
  output O7,
  output O8
);

  wire _1_pin3, _1_pin4, _1_pin5, _1_pin6, _2_pin3, _2_pin4, _2_pin5, _2_pin6;

  _74173 _1 (
    .pin1(1'b0), .pin2(1'b0), .pin3(_1_pin3), .pin4(_1_pin4), .pin5(_1_pin5), .pin6(_1_pin6), .pin7(CLK),
    .pin8(GND), .pin9(Load), .pin10(Load), .pin11(D4), .pin12(D3), .pin13(D2), .pin14(D1), .pin15(CLR),
    .pin16(VCC));
  _74173 _2 (
    .pin1(1'b0), .pin2(1'b0), .pin3(_2_pin3), .pin4(_2_pin4), .pin5(_2_pin5), .pin6(_2_pin6), .pin7(CLK),
    .pin8(GND), .pin9(Load), .pin10(Load), .pin11(D8), .pin12(D7), .pin13(D6), .pin14(D5), .pin15(CLR),
    .pin16(VCC));
  PowerSupply powersupply_1 (.VDD(VCC), .GND(GND));
  PullDown pulldown_1 (.out(_1_pin4));
  PullDown pulldown_2 (.out(_1_pin3));
  PullDown pulldown_3 (.out(_1_pin5));
  PullDown pulldown_4 (.out(_1_pin6));
  PullDown pulldown_5 (.out(_2_pin3));
  PullDown pulldown_6 (.out(_2_pin4));
  _74245 _74245_1 (
    .pin1(VCC), .pin2(_1_pin3), .pin3(_1_pin4), .pin4(_1_pin5), .pin5(_1_pin6), .pin6(_2_pin3),
    .pin7(_2_pin4), .pin8(_2_pin5), .pin9(_2_pin6), .pin10(GND), .pin11(O8), .pin12(O7), .pin13(O6),
    .pin14(O5), .pin15(O4), .pin16(O3), .pin17(O2), .pin18(O1), .pin19(Enable), .pin20(VCC));
  PullDown pulldown_7 (.out(_2_pin5));
  PullDown pulldown_8 (.out(_2_pin6));

  // Other names for the same wires on the sheet: _1 = Enable

  // Notes on the sheet:
  //   VCC: default 1
  //   Load: default 1
  //   Enable: default 1
endmodule
