// Digital circuit Clock Circut.dig as structural Verilog
module Clock_Circut (
  input  Clock_In,
  input  Select,
  input  HLT,
  input  Clock_Step,
  output Clock_Out
);

  wire and_1_out, and_2_out, not_1_out, not_2_out, or_1_out;

  and and_1 (and_1_out, Clock_In, Select);
  not not_1 (not_1_out, Select);
  and and_2 (and_2_out, not_1_out, Clock_Step);
  not not_2 (not_2_out, HLT);
  or or_1 (or_1_out, and_1_out, and_2_out);
  and and_3 (Clock_Out, or_1_out, not_2_out);

  // Notes on the sheet:
  //   Clock_In: Hz: 5
  //   Select: default 1
endmodule
