// Digital circuit D Flip-flop.dig as structural Verilog
module D_Flip_flop (
  input  D,
  input  Clk,
  output Q,
  output Q_I
);

  wire and_1_out, and_2_out, and_pulse_1_b, not_1_out;

  not not_1 (not_1_out, D);
  And_Pulse and_pulse_1 (.A(Clk), .B(and_pulse_1_b));
  and and_1 (and_1_out, not_1_out, and_pulse_1_b);
  and and_2 (and_2_out, and_pulse_1_b, D);
  nor nor_1 (Q, and_1_out, Q_I);
  nor nor_2 (Q_I, Q, and_2_out);
endmodule
