// Digital circuit D Latch.dig as structural Verilog
module D_Latch (
  input  D,
  input  Enable,
  output Q,
  output Q_I
);

  wire and_1_out, and_2_out, not_1_out;

  not not_1 (not_1_out, D);
  and and_1 (and_1_out, not_1_out, Enable);
  and and_2 (and_2_out, Enable, D);
  nor nor_1 (Q, and_1_out, Q_I);
  nor nor_2 (Q_I, Q, and_2_out);
endmodule
