// Digital circuit SR Latch with Enable.dig as structural Verilog
module SR_Latch_with_Enable (
  input  Reset,
  input  Enable,
  input  Set,
  output Q,
  output Q_I
);

  wire and_1_out, and_2_out;

  and and_1 (and_1_out, Reset, Enable);
  and and_2 (and_2_out, Enable, Set);
  nor nor_1 (Q, and_1_out, Q_I);
  nor nor_2 (Q_I, Q, and_2_out);
endmodule
